// Logisim project D锁存器翻转.circ as structural Verilog: 4 circuits, main circuit main
module main (
  input  en,
  input  reset,
  output Q,
  output Q1
);

  wire and_1_out, and_2_out, or_1_out;

  and and_1 (and_1_out, Q1, ~reset, en);  // AND_Gate
  and and_2 (and_2_out, en, ~Q1);  // AND_Gate
  or or_1 (or_1_out, and_2_out, reset);
  SRlatch srlatch_1 (.S(and_1_out), .R(or_1_out), .Q(Q), .Q1(Q1));
endmodule

module SRlatch (
  input  S,
  input  R,
  output Q,
  output Q1
);

  nor nor_1 (Q, R, Q1);
  nor nor_2 (Q1, Q, S);
endmodule

module DLatch (
  input  D,
  input  en,
  output Q,
  output Q1
);

  wire and_1_out, and_2_out;

  and and_1 (and_1_out, D, en);
  and and_2 (and_2_out, en, ~D);  // AND_Gate
  SRlatch srlatch_1 (.S(and_1_out), .R(and_2_out), .Q(Q), .Q1(Q1));
endmodule

module D_Latch_with_Asynchronous_Reset (
  input  D,
  input  en,
  input  reset,
  output Q,
  output Q1
);

  wire and_1_out, and_2_out, or_1_out;

  and and_1 (and_1_out, D, ~reset, en);  // AND_Gate
  and and_2 (and_2_out, en, ~D);  // AND_Gate
  or or_1 (or_1_out, and_2_out, reset);
  SRlatch srlatch_1 (.S(and_1_out), .R(or_1_out), .Q(Q), .Q1(Q1));
endmodule
