// Logisim project Switchable_7Segment_Decoder.circ as structural Verilog: 6 circuits, main circuit main
module main (
);

  wire a_out, and_1_out, and_2_out, and_3_out, and_4_out, and_5_out, and_6_out, and_7_out, and_8_out,
       and_9_out, and_10_out, and_11_out, and_12_out, and_13_out, and_14_out, b_out,
       bcd_to_7segment_decoder_1_a2, bcd_to_7segment_decoder_1_b2, bcd_to_7segment_decoder_1_c2,
       bcd_to_7segment_decoder_1_d2, bcd_to_7segment_decoder_1_e2, bcd_to_7segment_decoder_1_f2,
       bcd_to_7segment_decoder_1_g2, c_out, d_out, dipswitch_1_sw5, e_out, f_out, g_out,
       hex_to_7segment_decoder_1_a1, hex_to_7segment_decoder_1_b1, hex_to_7segment_decoder_1_c1,
       hex_to_7segment_decoder_1_d1, hex_to_7segment_decoder_1_e1, hex_to_7segment_decoder_1_f1,
       hex_to_7segment_decoder_1_g1;
  wire [3:0] dipswitch_1_sw4;

  DipSwitch #(.number(5)) dipswitch_1 (
    .sw1(dipswitch_1_sw4[3]), .sw2(dipswitch_1_sw4[2]), .sw3(dipswitch_1_sw4[1]), .sw4(dipswitch_1_sw4[0]),
    .sw5(dipswitch_1_sw5));
  BCD_to_7Segment_Decoder bcd_to_7segment_decoder_1 (
    .in_1(dipswitch_1_sw4), .a2(bcd_to_7segment_decoder_1_a2), .b2(bcd_to_7segment_decoder_1_b2),
    .c2(bcd_to_7segment_decoder_1_c2), .d2(bcd_to_7segment_decoder_1_d2), .e2(bcd_to_7segment_decoder_1_e2),
    .f2(bcd_to_7segment_decoder_1_f2), .g2(bcd_to_7segment_decoder_1_g2));
  Hex_to_7Segment_Decoder hex_to_7segment_decoder_1 (
    .in_1(dipswitch_1_sw4), .a1(hex_to_7segment_decoder_1_a1), .b1(hex_to_7segment_decoder_1_b1),
    .c1(hex_to_7segment_decoder_1_c1), .d1(hex_to_7segment_decoder_1_d1), .e1(hex_to_7segment_decoder_1_e1),
    .f1(hex_to_7segment_decoder_1_f1), .g1(hex_to_7segment_decoder_1_g1));
  and and_1 (and_1_out, bcd_to_7segment_decoder_1_a2, ~dipswitch_1_sw5);  // AND_Gate
  and and_2 (and_2_out, bcd_to_7segment_decoder_1_b2, ~dipswitch_1_sw5);  // AND_Gate
  and and_3 (and_3_out, bcd_to_7segment_decoder_1_c2, ~dipswitch_1_sw5);  // AND_Gate
  and and_4 (and_4_out, bcd_to_7segment_decoder_1_d2, ~dipswitch_1_sw5);  // AND_Gate
  and and_5 (and_5_out, bcd_to_7segment_decoder_1_e2, ~dipswitch_1_sw5);  // AND_Gate
  and and_6 (and_6_out, bcd_to_7segment_decoder_1_f2, ~dipswitch_1_sw5);  // AND_Gate
  and and_7 (and_7_out, bcd_to_7segment_decoder_1_g2, ~dipswitch_1_sw5);  // AND_Gate
  and and_8 (and_8_out, hex_to_7segment_decoder_1_a1, dipswitch_1_sw5);
  and and_9 (and_9_out, hex_to_7segment_decoder_1_b1, dipswitch_1_sw5);
  and and_10 (and_10_out, hex_to_7segment_decoder_1_c1, dipswitch_1_sw5);
  and and_11 (and_11_out, hex_to_7segment_decoder_1_d1, dipswitch_1_sw5);
  and and_12 (and_12_out, hex_to_7segment_decoder_1_e1, dipswitch_1_sw5);
  and and_13 (and_13_out, hex_to_7segment_decoder_1_f1, dipswitch_1_sw5);
  and and_14 (and_14_out, hex_to_7segment_decoder_1_g1, dipswitch_1_sw5);
  or a (a_out, and_1_out, and_8_out);
  or b (b_out, and_2_out, and_9_out);
  or c (c_out, and_3_out, and_10_out);
  or d (d_out, and_4_out, and_11_out);
  or e (e_out, and_5_out, and_12_out);
  or f (f_out, and_6_out, and_13_out);
  or g (g_out, and_7_out, and_14_out);
  _7_Segment_Display u_7_segment_display_1 (
    .g(g_out), .f(f_out), .a(a_out), .b(b_out), .e(e_out), .d(d_out), .c(c_out));  // open: dp
endmodule

module BCD_to_7Segment_Decoder (
  input  [3:0] in_1,
  output a2,
  output b2,
  output c2,
  output d2,
  output e2,
  output f2,
  output g2
);

  wire [15:0] decoder4_16_1_out_5;

  decoder4_16 decoder4_16_1 (.in_1(in_1[0]), .in_2(in_1[1]), .in_3(in_1[2]), .Y4(in_1[3]), .out_5(decoder4_16_1_out_5));
  or d (d2, decoder4_16_1_out_5[0], decoder4_16_1_out_5[2], decoder4_16_1_out_5[3], decoder4_16_1_out_5[5], decoder4_16_1_out_5[6], decoder4_16_1_out_5[8], decoder4_16_1_out_5[9]);
  or e (e2, decoder4_16_1_out_5[0], decoder4_16_1_out_5[2], decoder4_16_1_out_5[6], decoder4_16_1_out_5[8]);
  or c (c2, decoder4_16_1_out_5[0], decoder4_16_1_out_5[1], decoder4_16_1_out_5[3], decoder4_16_1_out_5[4], decoder4_16_1_out_5[5], decoder4_16_1_out_5[6], decoder4_16_1_out_5[7], decoder4_16_1_out_5[8], decoder4_16_1_out_5[9]);
  or g (g2, decoder4_16_1_out_5[2], decoder4_16_1_out_5[3], decoder4_16_1_out_5[4], decoder4_16_1_out_5[6], decoder4_16_1_out_5[8], decoder4_16_1_out_5[9], decoder4_16_1_out_5[5]);
  or f (f2, decoder4_16_1_out_5[0], decoder4_16_1_out_5[4], decoder4_16_1_out_5[5], decoder4_16_1_out_5[6], decoder4_16_1_out_5[8], decoder4_16_1_out_5[9]);
  or a (a2, decoder4_16_1_out_5[0], decoder4_16_1_out_5[2], decoder4_16_1_out_5[3], decoder4_16_1_out_5[5], decoder4_16_1_out_5[6], decoder4_16_1_out_5[7], decoder4_16_1_out_5[8], decoder4_16_1_out_5[9]);
  or b (b2, decoder4_16_1_out_5[9], decoder4_16_1_out_5[8], decoder4_16_1_out_5[7], decoder4_16_1_out_5[4], decoder4_16_1_out_5[3], decoder4_16_1_out_5[2], decoder4_16_1_out_5[1], decoder4_16_1_out_5[0]);
endmodule

module Hex_to_7Segment_Decoder (
  input  [3:0] in_1,
  output a1,
  output b1,
  output c1,
  output d1,
  output e1,
  output f1,
  output g1
);

  wire [15:0] decoder4_16_1_out_5;

  decoder4_16 decoder4_16_1 (.in_1(in_1[0]), .in_2(in_1[1]), .in_3(in_1[2]), .Y4(in_1[3]), .out_5(decoder4_16_1_out_5));
  or d (d1, decoder4_16_1_out_5[0], decoder4_16_1_out_5[2], decoder4_16_1_out_5[3], decoder4_16_1_out_5[5], decoder4_16_1_out_5[6], decoder4_16_1_out_5[14], decoder4_16_1_out_5[8], decoder4_16_1_out_5[9], decoder4_16_1_out_5[11], decoder4_16_1_out_5[12], decoder4_16_1_out_5[13]);
  or e (e1, decoder4_16_1_out_5[0], decoder4_16_1_out_5[2], decoder4_16_1_out_5[6], decoder4_16_1_out_5[8], decoder4_16_1_out_5[10], decoder4_16_1_out_5[11], decoder4_16_1_out_5[12], decoder4_16_1_out_5[13], decoder4_16_1_out_5[15], decoder4_16_1_out_5[14]);
  or c (c1, decoder4_16_1_out_5[0], decoder4_16_1_out_5[1], decoder4_16_1_out_5[3], decoder4_16_1_out_5[4], decoder4_16_1_out_5[11], decoder4_16_1_out_5[5], decoder4_16_1_out_5[7], decoder4_16_1_out_5[8], decoder4_16_1_out_5[9], decoder4_16_1_out_5[10], decoder4_16_1_out_5[13], decoder4_16_1_out_5[6]);
  or g (g1, decoder4_16_1_out_5[14], decoder4_16_1_out_5[8], decoder4_16_1_out_5[2], decoder4_16_1_out_5[3], decoder4_16_1_out_5[4], decoder4_16_1_out_5[6], decoder4_16_1_out_5[15], decoder4_16_1_out_5[9], decoder4_16_1_out_5[10], decoder4_16_1_out_5[11], decoder4_16_1_out_5[13], decoder4_16_1_out_5[5]);
  or f (f1, decoder4_16_1_out_5[0], decoder4_16_1_out_5[4], decoder4_16_1_out_5[5], decoder4_16_1_out_5[6], decoder4_16_1_out_5[8], decoder4_16_1_out_5[14], decoder4_16_1_out_5[9], decoder4_16_1_out_5[10], decoder4_16_1_out_5[11], decoder4_16_1_out_5[12], decoder4_16_1_out_5[15]);
  or a (a1, decoder4_16_1_out_5[15], decoder4_16_1_out_5[0], decoder4_16_1_out_5[2], decoder4_16_1_out_5[3], decoder4_16_1_out_5[5], decoder4_16_1_out_5[6], decoder4_16_1_out_5[7], decoder4_16_1_out_5[8], decoder4_16_1_out_5[9], decoder4_16_1_out_5[10], decoder4_16_1_out_5[12], decoder4_16_1_out_5[14]);
  or b (b1, decoder4_16_1_out_5[13], decoder4_16_1_out_5[10], decoder4_16_1_out_5[9], decoder4_16_1_out_5[8], decoder4_16_1_out_5[7], decoder4_16_1_out_5[4], decoder4_16_1_out_5[3], decoder4_16_1_out_5[2], decoder4_16_1_out_5[1], decoder4_16_1_out_5[0]);
endmodule

module decoder2_4 (
  input  in_1,
  input  in_2,
  output [3:0] out_3
);

  and and_1 (out_3[3], in_1, in_2);
  and and_2 (out_3[2], in_1, ~in_2);  // AND_Gate
  and and_3 (out_3[1], ~in_1, in_2);  // AND_Gate
  and and_4 (out_3[0], ~in_1, ~in_2);  // AND_Gate
endmodule

module decoder3_8 (
  input  Y0,
  input  Y1,
  input  Y2,
  output [7:0] out_4
);

  wire [3:0] decoder2_4_1_out_3, decoder2_4_2_out_3;

  decoder2_4 decoder2_4_1 (.in_1(Y1), .in_2(Y0), .out_3(decoder2_4_1_out_3));
  decoder2_4 decoder2_4_2 (.in_1(Y1), .in_2(Y0), .out_3(decoder2_4_2_out_3));
  assign out_4[3:0] = decoder2_4_1_out_3 & ~{4{Y2}};  // AND_Gate and_1, 4 bits wide
  assign out_4[7:4] = decoder2_4_2_out_3 & {4{Y2}};  // AND_Gate and_2, 4 bits wide
endmodule

module decoder4_16 (
  input  in_1,
  input  in_2,
  input  in_3,
  input  Y4,
  output [15:0] out_5
);

  wire [7:0] decoder3_8_1_out_4, decoder3_8_2_out_4;

  decoder3_8 decoder3_8_1 (.Y0(in_1), .Y1(in_2), .Y2(in_3), .out_4(decoder3_8_1_out_4));
  decoder3_8 decoder3_8_2 (.Y0(in_1), .Y1(in_2), .Y2(in_3), .out_4(decoder3_8_2_out_4));
  assign out_5[7:0] = decoder3_8_1_out_4 & ~{8{Y4}};  // AND_Gate and_1, 8 bits wide
  assign out_5[15:8] = decoder3_8_2_out_4 & {8{Y4}};  // AND_Gate and_2, 8 bits wide
endmodule
