// Logisim project T_FlipFlop_From_DFF.circ as structural Verilog: 7 circuits, main circuit main
module main (
  input  in_1,
  input  in_2,
  output out_3
);

  wire not_1_out;

  D_FlipFlop_SyncReset d_flipflop_syncreset_1 (.D(not_1_out), .RESET(in_1), .CLK(in_2), .Q(out_3));
  not not_1 (not_1_out, out_3);
endmodule

module SRlatch (
  input  S,
  input  R,
  output Q,
  output Q1
);

  nor nor_1 (Q, R, Q1);
  nor nor_2 (Q1, Q, S);
endmodule

module DLatch (
  input  D,
  input  en,
  output Q,
  output Q1
);

  wire and_1_out, and_2_out;

  and and_1 (and_1_out, D, en);
  and and_2 (and_2_out, en, ~D);  // AND_Gate
  SRlatch srlatch_1 (.S(and_1_out), .R(and_2_out), .Q(Q), .Q1(Q1));
endmodule

module D_Latch_AsyncReset (
  input  D,
  input  en,
  input  reset,
  output Q,
  output Q1
);

  wire and_1_out, and_2_out, or_1_out;

  and and_1 (and_1_out, D, ~reset, en);  // AND_Gate
  and and_2 (and_2_out, en, ~D);  // AND_Gate
  or or_1 (or_1_out, and_2_out, reset);
  SRlatch srlatch_1 (.S(and_1_out), .R(or_1_out), .Q(Q), .Q1(Q1));
endmodule

module D_Flip_Flop (
  input  D,
  input  clk,
  output Q
);

  wire dlatch_1_q, not_1_out;

  not not_1 (not_1_out, clk);
  DLatch dlatch_1 (.D(D), .en(not_1_out), .Q(dlatch_1_q));  // open: Q1
  DLatch dlatch_2 (.D(dlatch_1_q), .en(clk), .Q(Q));  // open: Q1
endmodule

module D_FlipFlop_SyncReset (
  input  D,
  input  RESET,
  input  CLK,
  output Q
);

  wire and_1_out;

  and and_1 (and_1_out, D, RESET);
  D_Flip_Flop d_flip_flop_1 (.D(and_1_out), .clk(CLK), .Q(Q));
endmodule

module D_FlipFlop_Enable (
  input  D,
  input  en,
  input  clk,
  output Q
);

  wire multiplexer_1_out;

  Multiplexer multiplexer_1 (.in0(Q), .in1(D), .out(multiplexer_1_out), .sel(en));
  D_Flip_Flop d_flip_flop_1 (.D(multiplexer_1_out), .clk(clk), .Q(Q));
endmodule
