// Logisim project adders.circ as structural Verilog: 15 circuits, main circuit TwosComplement_Adder_8bit
module TwosComplement_Adder_8bit (
  input  [7:0] in_1,
  input  [7:0] in_2,
  output [7:0] out_3
);

  wire and_1_out, and_2_out, or_1_out;

  Adder adder_1 (.a(in_2), .b(in_1), .out(out_3));  // open: cin, cout
  and and_1 (and_1_out, ~out_3[7], in_1[7], in_2[7]);  // AND_Gate
  and and_2 (and_2_out, out_3[7], ~in_1[7], ~in_2[7]);  // AND_Gate
  or or_1 (or_1_out, and_1_out, and_2_out);
  LED led_1 (.in(or_1_out));
endmodule

module halfadder (
  input  A,
  input  B,
  output S,
  output C
);

  and and_1 (C, A, B);
  xor xor_1 (S, A, B);
endmodule

module fulladder (
  input  A,
  input  B,
  input  Cin,
  output S,
  output Cout
);

  wire halfadder_1_c, halfadder_1_s, halfadder_2_c;

  halfadder halfadder_1 (.A(A), .B(B), .S(halfadder_1_s), .C(halfadder_1_c));
  halfadder halfadder_2 (.A(halfadder_1_s), .B(Cin), .S(S), .C(halfadder_2_c));
  or or_1 (Cout, halfadder_2_c, halfadder_1_c);
endmodule

module decoder2_4 (
  input  in_1,
  input  in_2,
  output [3:0] out_3
);

  and and_1 (out_3[3], in_1, in_2);
  and and_2 (out_3[2], in_1, ~in_2);  // AND_Gate
  and and_3 (out_3[1], ~in_1, in_2);  // AND_Gate
  and and_4 (out_3[0], ~in_1, ~in_2);  // AND_Gate
endmodule

module decoder3_8 (
  input  Y0,
  input  Y1,
  input  Y2,
  output [7:0] out_4
);

  wire [3:0] decoder2_4_1_out_3, decoder2_4_2_out_3;

  decoder2_4 decoder2_4_1 (.in_1(Y1), .in_2(Y0), .out_3(decoder2_4_1_out_3));
  decoder2_4 decoder2_4_2 (.in_1(Y1), .in_2(Y0), .out_3(decoder2_4_2_out_3));
  assign out_4[3:0] = decoder2_4_1_out_3 & ~{4{Y2}};  // AND_Gate and_1, 4 bits wide
  assign out_4[7:4] = decoder2_4_2_out_3 & {4{Y2}};  // AND_Gate and_2, 4 bits wide
endmodule

module decoder4_16 (
  input  in_1,
  input  in_2,
  input  in_3,
  input  Y4,
  output [15:0] out_5
);

  wire [7:0] decoder3_8_1_out_4, decoder3_8_2_out_4;

  decoder3_8 decoder3_8_1 (.Y0(in_1), .Y1(in_2), .Y2(in_3), .out_4(decoder3_8_1_out_4));
  decoder3_8 decoder3_8_2 (.Y0(in_1), .Y1(in_2), .Y2(in_3), .out_4(decoder3_8_2_out_4));
  assign out_5[7:0] = decoder3_8_1_out_4 & ~{8{Y4}};  // AND_Gate and_1, 8 bits wide
  assign out_5[15:8] = decoder3_8_2_out_4 & {8{Y4}};  // AND_Gate and_2, 8 bits wide
endmodule

module Hex_to_7Segment_Decoder (
  input  [3:0] in_1,
  output a1,
  output b1,
  output c1,
  output d1,
  output e1,
  output f1,
  output g1
);

  wire [15:0] decoder4_16_1_out_5;

  decoder4_16 decoder4_16_1 (.in_1(in_1[0]), .in_2(in_1[1]), .in_3(in_1[2]), .Y4(in_1[3]), .out_5(decoder4_16_1_out_5));
  or d (d1, decoder4_16_1_out_5[0], decoder4_16_1_out_5[2], decoder4_16_1_out_5[3], decoder4_16_1_out_5[5], decoder4_16_1_out_5[6], decoder4_16_1_out_5[14], decoder4_16_1_out_5[8], decoder4_16_1_out_5[9], decoder4_16_1_out_5[11], decoder4_16_1_out_5[12], decoder4_16_1_out_5[13]);
  or e (e1, decoder4_16_1_out_5[0], decoder4_16_1_out_5[2], decoder4_16_1_out_5[6], decoder4_16_1_out_5[8], decoder4_16_1_out_5[10], decoder4_16_1_out_5[11], decoder4_16_1_out_5[12], decoder4_16_1_out_5[13], decoder4_16_1_out_5[15], decoder4_16_1_out_5[14]);
  or c (c1, decoder4_16_1_out_5[0], decoder4_16_1_out_5[1], decoder4_16_1_out_5[3], decoder4_16_1_out_5[4], decoder4_16_1_out_5[11], decoder4_16_1_out_5[5], decoder4_16_1_out_5[7], decoder4_16_1_out_5[8], decoder4_16_1_out_5[9], decoder4_16_1_out_5[10], decoder4_16_1_out_5[13], decoder4_16_1_out_5[6]);
  or g (g1, decoder4_16_1_out_5[14], decoder4_16_1_out_5[8], decoder4_16_1_out_5[2], decoder4_16_1_out_5[3], decoder4_16_1_out_5[4], decoder4_16_1_out_5[6], decoder4_16_1_out_5[15], decoder4_16_1_out_5[9], decoder4_16_1_out_5[10], decoder4_16_1_out_5[11], decoder4_16_1_out_5[13], decoder4_16_1_out_5[5]);
  or f (f1, decoder4_16_1_out_5[0], decoder4_16_1_out_5[4], decoder4_16_1_out_5[5], decoder4_16_1_out_5[6], decoder4_16_1_out_5[8], decoder4_16_1_out_5[14], decoder4_16_1_out_5[9], decoder4_16_1_out_5[10], decoder4_16_1_out_5[11], decoder4_16_1_out_5[12], decoder4_16_1_out_5[15]);
  or a (a1, decoder4_16_1_out_5[15], decoder4_16_1_out_5[0], decoder4_16_1_out_5[2], decoder4_16_1_out_5[3], decoder4_16_1_out_5[5], decoder4_16_1_out_5[6], decoder4_16_1_out_5[7], decoder4_16_1_out_5[8], decoder4_16_1_out_5[9], decoder4_16_1_out_5[10], decoder4_16_1_out_5[12], decoder4_16_1_out_5[14]);
  or b (b1, decoder4_16_1_out_5[13], decoder4_16_1_out_5[10], decoder4_16_1_out_5[9], decoder4_16_1_out_5[8], decoder4_16_1_out_5[7], decoder4_16_1_out_5[4], decoder4_16_1_out_5[3], decoder4_16_1_out_5[2], decoder4_16_1_out_5[1], decoder4_16_1_out_5[0]);
endmodule

module RCA_4bit (
  input  in_1,
  input  in_2,
  input  in_3,
  input  in_4,
  input  in_5,
  input  in_6,
  input  in_7,
  input  in_8
);

  wire fulladder_1_cout, fulladder_2_cout, fulladder_3_cout, halfadder_1_c, hex_to_7segment_decoder_1_a1,
       hex_to_7segment_decoder_1_b1, hex_to_7segment_decoder_1_c1, hex_to_7segment_decoder_1_d1,
       hex_to_7segment_decoder_1_e1, hex_to_7segment_decoder_1_f1, hex_to_7segment_decoder_1_g1,
       hex_to_7segment_decoder_2_a1, hex_to_7segment_decoder_2_b1, hex_to_7segment_decoder_2_c1,
       hex_to_7segment_decoder_2_d1, hex_to_7segment_decoder_2_e1, hex_to_7segment_decoder_2_f1,
       hex_to_7segment_decoder_2_g1, hex_to_7segment_decoder_3_a1, hex_to_7segment_decoder_3_b1,
       hex_to_7segment_decoder_3_c1, hex_to_7segment_decoder_3_d1, hex_to_7segment_decoder_3_e1,
       hex_to_7segment_decoder_3_f1, hex_to_7segment_decoder_3_g1;
  wire [3:0] halfadder_1_s;

  fulladder fulladder_1 (.A(in_2), .B(in_1), .Cin(fulladder_2_cout), .S(halfadder_1_s[3]), .Cout(fulladder_1_cout));
  fulladder fulladder_2 (.A(in_4), .B(in_3), .Cin(fulladder_3_cout), .S(halfadder_1_s[2]), .Cout(fulladder_2_cout));
  fulladder fulladder_3 (.A(in_6), .B(in_5), .Cin(halfadder_1_c), .S(halfadder_1_s[1]), .Cout(fulladder_3_cout));
  halfadder halfadder_1 (.A(in_8), .B(in_7), .S(halfadder_1_s[0]), .C(halfadder_1_c));
  LED led_1 (.in(fulladder_1_cout));
  Hex_to_7Segment_Decoder hex_to_7segment_decoder_1 (
    .in_1(halfadder_1_s), .a1(hex_to_7segment_decoder_1_a1), .b1(hex_to_7segment_decoder_1_b1),
    .c1(hex_to_7segment_decoder_1_c1), .d1(hex_to_7segment_decoder_1_d1), .e1(hex_to_7segment_decoder_1_e1),
    .f1(hex_to_7segment_decoder_1_f1), .g1(hex_to_7segment_decoder_1_g1));
  _7_Segment_Display u_7_segment_display_1 (
    .g(hex_to_7segment_decoder_1_g1), .f(hex_to_7segment_decoder_1_f1), .a(hex_to_7segment_decoder_1_a1),
    .b(hex_to_7segment_decoder_1_b1), .e(hex_to_7segment_decoder_1_e1), .d(hex_to_7segment_decoder_1_d1),
    .c(hex_to_7segment_decoder_1_c1));  // open: dp
  Hex_to_7Segment_Decoder hex_to_7segment_decoder_2 (
    .in_1({in_2, in_4, in_6, in_8}), .a1(hex_to_7segment_decoder_2_a1), .b1(hex_to_7segment_decoder_2_b1),
    .c1(hex_to_7segment_decoder_2_c1), .d1(hex_to_7segment_decoder_2_d1), .e1(hex_to_7segment_decoder_2_e1),
    .f1(hex_to_7segment_decoder_2_f1), .g1(hex_to_7segment_decoder_2_g1));
  Hex_to_7Segment_Decoder hex_to_7segment_decoder_3 (
    .in_1({in_1, in_3, in_5, in_7}), .a1(hex_to_7segment_decoder_3_a1), .b1(hex_to_7segment_decoder_3_b1),
    .c1(hex_to_7segment_decoder_3_c1), .d1(hex_to_7segment_decoder_3_d1), .e1(hex_to_7segment_decoder_3_e1),
    .f1(hex_to_7segment_decoder_3_f1), .g1(hex_to_7segment_decoder_3_g1));
  _7_Segment_Display u_7_segment_display_2 (
    .g(hex_to_7segment_decoder_2_g1), .f(hex_to_7segment_decoder_2_f1), .a(hex_to_7segment_decoder_2_a1),
    .b(hex_to_7segment_decoder_2_b1), .e(hex_to_7segment_decoder_2_e1), .d(hex_to_7segment_decoder_2_d1),
    .c(hex_to_7segment_decoder_2_c1));  // open: dp
  _7_Segment_Display u_7_segment_display_3 (
    .g(hex_to_7segment_decoder_3_g1), .f(hex_to_7segment_decoder_3_f1), .a(hex_to_7segment_decoder_3_a1),
    .b(hex_to_7segment_decoder_3_b1), .e(hex_to_7segment_decoder_3_e1), .d(hex_to_7segment_decoder_3_d1),
    .c(hex_to_7segment_decoder_3_c1));  // open: dp
endmodule

module Half_Subtractor (
  input  A,
  input  B,
  output D,
  output Bout
);

  wire and_1_out, and_2_out, not_1_out, not_2_out;

  not not_1 (not_1_out, A);
  not not_2 (not_2_out, B);
  and and_1 (and_1_out, not_1_out, B);
  and and_2 (and_2_out, A, not_2_out);
  and and_3 (Bout, not_1_out, B);
  or or_1 (D, and_1_out, and_2_out);
endmodule

module Full_Subtractor (
  input  A,
  input  B,
  input  Bin,
  output D,
  output Bout
);

  wire half_subtractor_1_bout, half_subtractor_1_d, half_subtractor_2_bout;

  Half_Subtractor half_subtractor_1 (.A(A), .B(B), .D(half_subtractor_1_d), .Bout(half_subtractor_1_bout));
  Half_Subtractor half_subtractor_2 (.A(half_subtractor_1_d), .B(Bin), .D(D), .Bout(half_subtractor_2_bout));
  or or_1 (Bout, half_subtractor_2_bout, half_subtractor_1_bout);
endmodule

module SignMagnitude_Adder_4bit (
  input  in_1,
  input  [3:0] in_2,
  input  in_3,
  input  [3:0] in_4
);

  wire adder_1_cout, and_1_out, and_2_out, and_3_out, and_4_out, or_1_out, subtractor_1_bout,
       subtractor_2_bout, xnor_1_out, xor_1_out, xor_2_out;
  wire [3:0] adder_1_out, multiplexer_1_out, multiplexer_2_out, subtractor_1_out, subtractor_2_out;

  _7_Segment_Display u_7_segment_display_1 (.g(in_1));  // open: f, a, b, e, d, c, dp
  _7_Segment_Display u_7_segment_display_2 (.g(in_3));  // open: f, a, b, e, d, c, dp
  Hex_Digit_Display hex_digit_display_1 (.value(in_2));  // open: dp
  xor xor_1 (xor_1_out, in_1, in_3);
  Hex_Digit_Display hex_digit_display_2 (.value(in_4));  // open: dp
  xor xor_2 (xor_2_out, in_1, in_3);
  and and_1 (and_1_out, in_1, in_3);
  Adder #(.width(4)) adder_1 (.a(in_2), .b(in_4), .out(adder_1_out), .cout(adder_1_cout));  // open: cin
  Subtractor #(.width(4)) subtractor_1 (
    .a(in_2), .b(in_4), .out(subtractor_1_out), .bout(subtractor_1_bout));  // open: bin
  Subtractor #(.width(4)) subtractor_2 (
    .a(in_4), .b(in_2), .out(subtractor_2_out), .bout(subtractor_2_bout));  // open: bin
  Multiplexer #(.width(4)) multiplexer_1 (
    .in0(subtractor_1_out), .in1(subtractor_2_out), .out(multiplexer_1_out), .sel(subtractor_1_bout));
  and and_2 (and_2_out, xor_2_out, in_3, subtractor_1_bout);
  and and_3 (and_3_out, xor_2_out, in_1, subtractor_2_bout);
  Multiplexer #(.width(4)) multiplexer_2 (
    .in0(adder_1_out), .in1(multiplexer_1_out), .out(multiplexer_2_out), .sel(xor_1_out));
  xnor xnor_1 (xnor_1_out, in_1, in_3);
  or or_1 (or_1_out, and_1_out, and_2_out, and_3_out);
  _7_Segment_Display u_7_segment_display_3 (.g(or_1_out));  // open: f, a, b, e, d, c, dp
  and and_4 (and_4_out, adder_1_cout, xnor_1_out);
  Hex_Digit_Display hex_digit_display_3 (.value(multiplexer_2_out));  // open: dp
  LED led_1 (.in(and_4_out));
endmodule

module OnesComplement_Adder_4bit (
  input  [3:0] in_1,
  input  [3:0] in_2,
  input  in_3,
  input  in_4,
  output out_5,
  output [3:0] out_6
);

  wire adder_1_cout, and_1_out, and_2_out, and_3_out, and_4_out, subtractor_1_bout, subtractor_2_bout,
       xnor_1_out, xor_1_out, xor_2_out;
  wire [3:0] adder_1_out, multiplexer_1_out, multiplexer_2_out, multiplexer_3_out, multiplexer_4_out,
       not_1_out, not_2_out, not_3_out, subtractor_1_out, subtractor_2_out;

  assign not_1_out = ~in_1;  // NOT_Gate not_1, 4 bits wide
  assign not_2_out = ~in_2;  // NOT_Gate not_2, 4 bits wide
  Multiplexer #(.width(4)) multiplexer_1 (.in0(in_1), .in1(not_1_out), .out(multiplexer_1_out), .sel(in_3));
  Multiplexer #(.width(4)) multiplexer_2 (.in0(in_2), .in1(not_2_out), .out(multiplexer_2_out), .sel(in_4));
  _7_Segment_Display u_7_segment_display_1 (.g(in_3));  // open: f, a, b, e, d, c, dp
  Hex_Digit_Display hex_digit_display_1 (.value(multiplexer_1_out));  // open: dp
  _7_Segment_Display u_7_segment_display_2 (.g(in_4));  // open: f, a, b, e, d, c, dp
  xor xor_1 (xor_1_out, in_3, in_4);
  Hex_Digit_Display hex_digit_display_2 (.value(multiplexer_2_out));  // open: dp
  xor xor_2 (xor_2_out, in_3, in_4);
  and and_1 (and_1_out, in_3, in_4);
  Adder #(.width(4)) adder_1 (
    .a(multiplexer_1_out), .b(multiplexer_2_out), .out(adder_1_out), .cout(adder_1_cout));  // open: cin
  Subtractor #(.width(4)) subtractor_1 (
    .a(multiplexer_1_out), .b(multiplexer_2_out), .out(subtractor_1_out), .bout(subtractor_1_bout));  // open: bin
  Subtractor #(.width(4)) subtractor_2 (
    .a(multiplexer_2_out), .b(multiplexer_1_out), .out(subtractor_2_out), .bout(subtractor_2_bout));  // open: bin
  and and_2 (and_2_out, xor_2_out, in_4, subtractor_1_bout);
  and and_3 (and_3_out, xor_2_out, in_3, subtractor_2_bout);
  Multiplexer #(.width(4)) multiplexer_3 (
    .in0(subtractor_1_out), .in1(subtractor_2_out), .out(multiplexer_3_out), .sel(subtractor_1_bout));
  Multiplexer #(.width(4)) multiplexer_4 (
    .in0(adder_1_out), .in1(multiplexer_3_out), .out(multiplexer_4_out), .sel(xor_1_out));
  assign not_3_out = ~multiplexer_4_out;  // NOT_Gate not_3, 4 bits wide
  xnor xnor_1 (xnor_1_out, in_3, in_4);
  or or_1 (out_5, and_1_out, and_2_out, and_3_out);
  _7_Segment_Display u_7_segment_display_3 (.g(out_5));  // open: f, a, b, e, d, c, dp
  Multiplexer #(.width(4)) multiplexer_5 (.in0(multiplexer_4_out), .in1(not_3_out), .out(out_6), .sel(out_5));
  and and_4 (and_4_out, adder_1_cout, xnor_1_out);
  Hex_Digit_Display hex_digit_display_3 (.value(multiplexer_4_out));  // open: dp
  LED led_1 (.in(and_4_out));
endmodule

module OnesComplement_Adder_8bit (
  input  [7:0] in_1,
  input  [7:0] in_2,
  output [7:0] out_3,
  output [7:0] out_4,
  output [7:0] out_5
);

  wire or_1_out;
  wire [7:0] adder_2_out, not_1_out;

  or or_1 (or_1_out, in_2[7], in_1[7]);
  Adder adder_1 (.a(in_1), .b(in_2), .out(out_3));  // open: cin, cout
  Adder adder_2 (.a(out_3), .b(8'h1), .out(adder_2_out));  // open: cin, cout
  Multiplexer #(.width(8)) multiplexer_1 (.in0(out_3), .in1(adder_2_out), .out(out_4), .sel(or_1_out));
  assign not_1_out = ~out_4;  // NOT_Gate not_1, 8 bits wide
  Multiplexer #(.width(8)) multiplexer_2 (.in0(out_4), .in1(not_1_out), .out(out_5), .sel(out_4[7]));
endmodule

module RBS_4bitp (
  input  A3,
  input  A2,
  input  A1,
  input  A0,
  input  B3,
  input  B2,
  input  B1,
  input  B0,
  output c,
  output out_10,
  output out_11,
  output out_12,
  output out_13,
  output out_14,
  output out_15,
  output d,
  output out_17,
  output out_18,
  output out_19,
  output out_20,
  output out_21,
  output out_22,
  output e,
  output out_24,
  output out_25,
  output out_26,
  output out_27,
  output out_28,
  output out_29,
  output Ledlight
);

  wire full_subtractor_2_bout, full_subtractor_3_bout, half_subtractor_1_bout, undriven, undriven_2,
       undriven_3, undriven_4, undriven_5, undriven_6, undriven_7;
  wire [3:0] half_subtractor_1_d;

  Full_Subtractor full_subtractor_1 (
    .A(A3), .B(B3), .Bin(full_subtractor_2_bout), .D(half_subtractor_1_d[3]), .Bout(Ledlight));
  Full_Subtractor full_subtractor_2 (
    .A(A2), .B(B2), .Bin(full_subtractor_3_bout), .D(half_subtractor_1_d[2]), .Bout(full_subtractor_2_bout));
  Full_Subtractor full_subtractor_3 (
    .A(A1), .B(B1), .Bin(half_subtractor_1_bout), .D(half_subtractor_1_d[1]), .Bout(full_subtractor_3_bout));
  Half_Subtractor half_subtractor_1 (.A(A0), .B(B0), .D(half_subtractor_1_d[0]), .Bout(half_subtractor_1_bout));
  Hex_to_7Segment_Decoder hex_to_7segment_decoder_1 (
    .in_1(half_subtractor_1_d), .a1(e), .b1(out_24), .c1(out_25), .d1(out_26), .e1(out_27), .f1(out_28),
    .g1(out_29));
  LED led_1 (.in(Ledlight));
  Hex_to_7Segment_Decoder hex_to_7segment_decoder_2 (
    .in_1({A3, A2, A1, A0}), .a1(c), .b1(out_10), .c1(out_11), .d1(out_12), .e1(out_13), .f1(out_14),
    .g1(out_15));
  Hex_to_7Segment_Decoder hex_to_7segment_decoder_3 (
    .in_1({B3, B2, B1, B0}), .a1(d), .b1(out_17), .c1(out_18), .d1(out_19), .e1(out_20), .f1(out_21),
    .g1(out_22));
  _7_Segment_Display u_7_segment_display_1 (
    .g(undriven_3), .f(undriven_4), .a(undriven), .b(undriven_2), .e(undriven_5), .d(undriven_6),
    .c(undriven_7));  // open: dp
endmodule

module RBS_4bit (
  input  [3:0] A,
  input  [3:0] B
);

  wire rbs_4bitp_1_c, rbs_4bitp_1_d, rbs_4bitp_1_ledlight, rbs_4bitp_1_out_10, rbs_4bitp_1_out_11,
       rbs_4bitp_1_out_12, rbs_4bitp_1_out_13, rbs_4bitp_1_out_14, rbs_4bitp_1_out_15, rbs_4bitp_1_out_17,
       rbs_4bitp_1_out_18, rbs_4bitp_1_out_19, rbs_4bitp_1_out_20, rbs_4bitp_1_out_21, rbs_4bitp_1_out_22;
  wire [6:0] multiplexer_1_out, rbs_4bitp_1_e, rbs_4bitp_2_e;

  RBS_4bitp rbs_4bitp_1 (
    .A3(A[3]), .A2(A[2]), .A1(A[1]), .A0(A[0]), .B3(B[3]), .B2(B[2]), .B1(B[1]), .B0(B[0]),
    .c(rbs_4bitp_1_c), .out_10(rbs_4bitp_1_out_10), .out_11(rbs_4bitp_1_out_11), .out_12(rbs_4bitp_1_out_12),
    .out_13(rbs_4bitp_1_out_13), .out_14(rbs_4bitp_1_out_14), .out_15(rbs_4bitp_1_out_15), .d(rbs_4bitp_1_d),
    .out_17(rbs_4bitp_1_out_17), .out_18(rbs_4bitp_1_out_18), .out_19(rbs_4bitp_1_out_19),
    .out_20(rbs_4bitp_1_out_20), .out_21(rbs_4bitp_1_out_21), .out_22(rbs_4bitp_1_out_22),
    .e(rbs_4bitp_1_e[0]), .out_24(rbs_4bitp_1_e[1]), .out_25(rbs_4bitp_1_e[2]), .out_26(rbs_4bitp_1_e[3]),
    .out_27(rbs_4bitp_1_e[4]), .out_28(rbs_4bitp_1_e[5]), .out_29(rbs_4bitp_1_e[6]),
    .Ledlight(rbs_4bitp_1_ledlight));
  _7_Segment_Display u_7_segment_display_1 (
    .g(rbs_4bitp_1_out_15), .f(rbs_4bitp_1_out_14), .a(rbs_4bitp_1_c), .b(rbs_4bitp_1_out_10),
    .e(rbs_4bitp_1_out_13), .d(rbs_4bitp_1_out_12), .c(rbs_4bitp_1_out_11));  // open: dp
  _7_Segment_Display u_7_segment_display_2 (
    .g(rbs_4bitp_1_out_22), .f(rbs_4bitp_1_out_21), .a(rbs_4bitp_1_d), .b(rbs_4bitp_1_out_17),
    .e(rbs_4bitp_1_out_20), .d(rbs_4bitp_1_out_19), .c(rbs_4bitp_1_out_18));  // open: dp
  RBS_4bitp rbs_4bitp_2 (
    .A3(B[3]), .A2(B[2]), .A1(B[1]), .A0(B[0]), .B3(A[3]), .B2(A[2]), .B1(A[1]), .B0(A[0]),
    .e(rbs_4bitp_2_e[0]), .out_24(rbs_4bitp_2_e[1]), .out_25(rbs_4bitp_2_e[2]), .out_26(rbs_4bitp_2_e[3]),
    .out_27(rbs_4bitp_2_e[4]), .out_28(rbs_4bitp_2_e[5]), .out_29(rbs_4bitp_2_e[6]));  // open: c, out_10, out_11, out_12, out_13, out_14, out_15, d, out_17, out_18, out_19, out_20, out_21, out_22, Ledlight
  Multiplexer #(.width(7)) multiplexer_1 (
    .in0(rbs_4bitp_1_e), .in1(rbs_4bitp_2_e), .out(multiplexer_1_out), .sel(rbs_4bitp_1_ledlight));
  _7_Segment_Display u_7_segment_display_3 (.g(rbs_4bitp_1_ledlight));  // open: f, a, b, e, d, c, dp
  _7_Segment_Display u_7_segment_display_4 (
    .g(multiplexer_1_out[6]), .f(multiplexer_1_out[5]), .a(multiplexer_1_out[0]), .b(multiplexer_1_out[1]),
    .e(multiplexer_1_out[4]), .d(multiplexer_1_out[3]), .c(multiplexer_1_out[2]));  // open: dp
endmodule
