// Logisim project register_8bit.circ as structural Verilog: 5 circuits, main circuit mainRegister_8bit
module mainRegister_8bit (
  input  c8,
  input  c7,
  input  c6,
  input  c5,
  input  c4,
  input  c3,
  input  c2,
  input  c1,
  input  reset,
  input  en,
  input  fuweien,
  input  clk,
  output out_13,
  output out_14,
  output out_15,
  output out_16,
  output out_17,
  output out_18,
  output out_19,
  output out_20
);

  wire and_1_out, and_2_out, and_3_out, and_4_out, and_5_out, and_6_out, and_7_out, and_8_out, or_1_out;

  or or_1 (or_1_out, en, fuweien);
  and and_1 (and_1_out, reset, c8);
  Enabled_DFF enabled_dff_1 (.en(or_1_out), .D(and_1_out), .clk(clk), .Q(out_13));
  and and_2 (and_2_out, reset, c7);
  Enabled_DFF enabled_dff_2 (.en(or_1_out), .D(and_2_out), .clk(clk), .Q(out_14));
  and and_3 (and_3_out, reset, c6);
  Enabled_DFF enabled_dff_3 (.en(or_1_out), .D(and_3_out), .clk(clk), .Q(out_15));
  and and_4 (and_4_out, reset, c5);
  Enabled_DFF enabled_dff_4 (.en(or_1_out), .D(and_4_out), .clk(clk), .Q(out_16));
  and and_5 (and_5_out, reset, c4);
  Enabled_DFF enabled_dff_5 (.en(or_1_out), .D(and_5_out), .clk(clk), .Q(out_17));
  and and_6 (and_6_out, reset, c3);
  Enabled_DFF enabled_dff_6 (.en(or_1_out), .D(and_6_out), .clk(clk), .Q(out_18));
  and and_7 (and_7_out, reset, c2);
  Enabled_DFF enabled_dff_7 (.en(or_1_out), .D(and_7_out), .clk(clk), .Q(out_19));
  and and_8 (and_8_out, reset, c1);
  Enabled_DFF enabled_dff_8 (.en(or_1_out), .D(and_8_out), .clk(clk), .Q(out_20));
endmodule

module SRlatch (
  input  S,
  input  R,
  output Q,
  output Q1
);

  nor nor_1 (Q, R, Q1);
  nor nor_2 (Q1, Q, S);
endmodule

module Dlatch (
  input  D,
  input  we,
  output out_3,
  output out_4
);

  wire and_1_out, and_2_out;

  and and_1 (and_1_out, D, we);
  and and_2 (and_2_out, we, ~D);  // AND_Gate
  SRlatch srlatch_1 (.S(and_1_out), .R(and_2_out), .Q(out_3), .Q1(out_4));
endmodule

module Enabled_DFF (
  input  en,
  input  D,
  input  clk,
  output Q
);

  wire dlatch_1_out_3, multiplexer_1_out, not_1_out;

  Multiplexer multiplexer_1 (.in0(Q), .in1(D), .out(multiplexer_1_out), .sel(en));
  not not_1 (not_1_out, clk);
  Dlatch dlatch_1 (.D(multiplexer_1_out), .we(not_1_out), .out_3(dlatch_1_out_3));  // open: out_4
  Dlatch dlatch_2 (.D(dlatch_1_out_3), .we(clk), .out_3(Q));  // open: out_4
endmodule

module register_4bit (
  input  c4,
  input  c3,
  input  c2,
  input  c1,
  input  en,
  input  clk,
  output out_7,
  output out_8,
  output out_9,
  output out_10
);

  Enabled_DFF enabled_dff_1 (.en(en), .D(c4), .clk(clk), .Q(out_7));
  Enabled_DFF enabled_dff_2 (.en(en), .D(c3), .clk(clk), .Q(out_8));
  Enabled_DFF enabled_dff_3 (.en(en), .D(c2), .clk(clk), .Q(out_9));
  Enabled_DFF enabled_dff_4 (.en(en), .D(c1), .clk(clk), .Q(out_10));
endmodule
