// Logisim project 四位输入编码器.circ as structural Verilog: 1 circuit, main circuit main
module main (
  input  A0,
  input  A1,
  input  A2,
  input  A3,
  output Y0,
  output Y1
);

  wire or_1_out, or_2_out;

  or or_1 (or_1_out, A1, A3);
  or or_2 (or_2_out, A2, A3);
  and and_1 (Y0, ~A0, or_1_out);  // AND_Gate
  and and_2 (Y1, ~A0, or_2_out);  // AND_Gate
endmodule
