// Logisim project 四选一多路选择器.circ as structural Verilog: 1 circuit, main circuit main
module main (
  input  ln3,
  input  ln2,
  input  ln1,
  input  ln0,
  input  Sel1,
  input  Sel0,
  output out_7
);

  wire and_1_out, and_2_out, and_3_out, and_4_out;

  and and_1 (and_1_out, Sel1, Sel0, ln3);
  and and_2 (and_2_out, Sel1, ~Sel0, ln2);  // AND_Gate
  and and_3 (and_3_out, ~Sel1, Sel0, ln1);  // AND_Gate
  and and_4 (and_4_out, ~Sel1, ~Sel0, ln0);  // AND_Gate
  or or_1 (out_7, and_1_out, and_2_out, and_3_out, and_4_out);
endmodule
