// Logisim project 编码器.circ as structural Verilog: 3 circuits, main circuit main
module main (
  input  [3:0] in_1,
  input  [3:0] in_2,
  input  [3:0] in_3,
  input  [3:0] in_4,
  output [2:0] out_5,
  output out_6
);

  wire [1:0] and_1_out, and_2_out, encoder4_2_1_y1, encoder4_2_2_y1, encoder4_2_3_y1, encoder4_2_4_y1,
       or_3_out, or_5_out;
  wire [1:1] encoder4_2_3_output1, encoder4_2_4_output1, or_1_out, or_2_out;
  wire [2:0] and_3_out;
  wire [2:2] encoder4_2_2_output1, or_4_out, or_6_out, or_7_out;

  encoder4_2 encoder4_2_1 (.A(in_1), .Y1(encoder4_2_1_y1));  // open: output1
  encoder4_2 encoder4_2_2 (.A(in_3), .Y1(encoder4_2_2_y1), .output1(encoder4_2_2_output1[2]));
  encoder4_2 encoder4_2_3 (.A(in_4), .Y1(encoder4_2_3_y1), .output1(encoder4_2_3_output1[1]));
  encoder4_2 encoder4_2_4 (.A(in_2), .Y1(encoder4_2_4_y1), .output1(encoder4_2_4_output1[1]));
  or or_1 (or_1_out[1], encoder4_2_4_y1[0], encoder4_2_4_y1[1]);
  or or_2 (or_2_out[1], encoder4_2_3_y1[0], encoder4_2_3_y1[1]);
  assign and_1_out = encoder4_2_1_y1 & ~{2{or_1_out[1]}} & ~{2{encoder4_2_4_output1[1]}};  // AND_Gate and_1, 2 bits wide
  assign and_2_out = encoder4_2_2_y1 & ~{2{or_2_out[1]}} & ~{2{encoder4_2_3_output1[1]}};  // AND_Gate and_2, 2 bits wide
  assign or_3_out = and_1_out | encoder4_2_4_y1;  // OR_Gate or_3, 2 bits wide
  or or_4 (or_4_out[2], encoder4_2_4_y1[0], encoder4_2_4_y1[1], encoder4_2_4_output1[1]);
  assign or_5_out = and_2_out | encoder4_2_3_y1;  // OR_Gate or_5, 2 bits wide
  or or_6 (or_6_out[2], encoder4_2_3_y1[0], encoder4_2_3_y1[1], encoder4_2_3_output1[1]);
  or or_7 (or_7_out[2], or_5_out[0], or_5_out[1], or_6_out[2]);
  assign and_3_out = {or_4_out[2], or_3_out} & ~{3{or_7_out[2]}} & ~{3{encoder4_2_2_output1[2]}};  // AND_Gate and_3, 3 bits wide
  or or_8 (out_6, or_5_out[0], or_5_out[1], or_6_out[2], encoder4_2_2_output1[2]);
  assign out_5 = and_3_out | {or_6_out[2], or_5_out};  // OR_Gate or_9, 3 bits wide
endmodule

module encoder4_2 (
  input  [3:0] A,
  output [1:0] Y1,
  output output1
);

  wire and_1_out, not_1_out;

  not not_1 (not_1_out, A[2]);
  or or_1 (Y1[1], A[2], A[3]);
  and and_1 (and_1_out, not_1_out, A[1]);
  or or_2 (Y1[0], and_1_out, A[3]);

  assign output1 = A[0];
endmodule

module encoder8_3 (
  input  [3:0] in_1,
  input  [3:0] in_2,
  output [1:0] out_3,
  output out_4
);

  wire [1:0] and_1_out, encoder4_2_1_y1, encoder4_2_2_y1;
  wire [1:1] encoder4_2_2_output1, or_1_out;

  encoder4_2 encoder4_2_1 (.A(in_1), .Y1(encoder4_2_1_y1));  // open: output1
  encoder4_2 encoder4_2_2 (.A(in_2), .Y1(encoder4_2_2_y1), .output1(encoder4_2_2_output1[1]));
  or or_1 (or_1_out[1], encoder4_2_2_y1[0], encoder4_2_2_y1[1]);
  assign and_1_out = encoder4_2_1_y1 & ~{2{or_1_out[1]}} & ~{2{encoder4_2_2_output1[1]}};  // AND_Gate and_1, 2 bits wide
  assign out_3 = and_1_out | encoder4_2_2_y1;  // OR_Gate or_2, 2 bits wide
  or or_3 (out_4, encoder4_2_2_y1[0], encoder4_2_2_y1[1], encoder4_2_2_output1[1]);
endmodule
