// Logisim project Decoder_2to4.circ as structural Verilog: 1 circuit, main circuit main
module main (
  input  A,
  input  B,
  output Y0,
  output Y1,
  output Y2,
  output Y3
);

  and and_1 (Y0, ~A, ~B);  // AND_Gate
  and and_2 (Y1, A, ~B);  // AND_Gate
  and and_3 (Y2, ~A, B);  // AND_Gate
  and and_4 (Y3, A, B);
endmodule
