// Logisim project decoder4_16.circ as structural Verilog: 3 circuits, main circuit main
module main (
  input  A,
  input  B,
  input  C,
  input  D,
  output [15:0] out_5
);

  wire [7:0] decoder3_8_1_out_4, decoder3_8_2_out_4;

  decoder3_8 decoder3_8_1 (.A(A), .B(B), .C(C), .out_4(decoder3_8_1_out_4));
  decoder3_8 decoder3_8_2 (.A(A), .B(B), .C(C), .out_4(decoder3_8_2_out_4));
  assign out_5[7:0] = decoder3_8_1_out_4 & ~{8{D}};  // AND_Gate and_1, 8 bits wide
  assign out_5[15:8] = decoder3_8_2_out_4 & {8{D}};  // AND_Gate and_2, 8 bits wide
endmodule

module decoder2_4 (
  input  A,
  input  B,
  output [3:0] out_3
);

  and and_1 (out_3[0], ~A, ~B);  // AND_Gate
  and and_2 (out_3[1], A, ~B);  // AND_Gate
  and and_3 (out_3[2], ~A, B);  // AND_Gate
  and and_4 (out_3[3], A, B);
endmodule

module decoder3_8 (
  input  A,
  input  B,
  input  C,
  output [7:0] out_4
);

  wire [3:0] decoder2_4_1_out_3, decoder2_4_2_out_3;

  decoder2_4 decoder2_4_1 (.A(A), .B(B), .out_3(decoder2_4_1_out_3));
  decoder2_4 decoder2_4_2 (.A(A), .B(B), .out_3(decoder2_4_2_out_3));
  assign out_4[3:0] = decoder2_4_1_out_3 & ~{4{C}};  // AND_Gate and_1, 4 bits wide
  assign out_4[7:4] = decoder2_4_2_out_3 & {4{C}};  // AND_Gate and_2, 4 bits wide
endmodule
