// Logisim project 8bit_Register_EN_SyncReset.circ as structural Verilog: 9 circuits, main circuit main
module main (
  input  D7,
  input  D6,
  input  D5,
  input  D4,
  input  D3,
  input  D2,
  input  D1,
  input  D0,
  input  reset,
  input  en,
  input  clk,
  output Q7,
  output Q6,
  output Q5,
  output Q4,
  output Q3,
  output Q2,
  output Q1,
  output Q0
);

  wire and_1_out, and_2_out, and_3_out, and_4_out, and_5_out, and_6_out, and_7_out, and_8_out;

  and and_1 (and_1_out, reset, D7);
  D_FlipFlop_Enable d_flipflop_enable_1 (.D(and_1_out), .en(en), .clk(clk), .Q(Q7));
  and and_2 (and_2_out, reset, D6);
  D_FlipFlop_Enable d_flipflop_enable_2 (.D(and_2_out), .en(en), .clk(clk), .Q(Q6));
  and and_3 (and_3_out, reset, D5);
  D_FlipFlop_Enable d_flipflop_enable_3 (.D(and_3_out), .en(en), .clk(clk), .Q(Q5));
  and and_4 (and_4_out, reset, D4);
  D_FlipFlop_Enable d_flipflop_enable_4 (.D(and_4_out), .en(en), .clk(clk), .Q(Q4));
  and and_5 (and_5_out, reset, D3);
  D_FlipFlop_Enable d_flipflop_enable_5 (.D(and_5_out), .en(en), .clk(clk), .Q(Q3));
  and and_6 (and_6_out, reset, D2);
  D_FlipFlop_Enable d_flipflop_enable_6 (.D(and_6_out), .en(en), .clk(clk), .Q(Q2));
  and and_7 (and_7_out, reset, D1);
  D_FlipFlop_Enable d_flipflop_enable_7 (.D(and_7_out), .en(en), .clk(clk), .Q(Q1));
  and and_8 (and_8_out, reset, D0);
  D_FlipFlop_Enable d_flipflop_enable_8 (.D(and_8_out), .en(en), .clk(clk), .Q(Q0));
endmodule

module SRlatch (
  input  S,
  input  R,
  output Q,
  output Q1
);

  nor nor_1 (Q, R, Q1);
  nor nor_2 (Q1, Q, S);
endmodule

module DLatch (
  input  D,
  input  en,
  output Q,
  output Q1
);

  wire and_1_out, and_2_out;

  and and_1 (and_1_out, D, en);
  and and_2 (and_2_out, en, ~D);  // AND_Gate
  SRlatch srlatch_1 (.S(and_1_out), .R(and_2_out), .Q(Q), .Q1(Q1));
endmodule

module Toggling_D_Latch_Reset (
  input  D,
  input  en,
  input  reset,
  output Q,
  output Q1
);

  wire and_1_out, and_2_out, or_1_out;

  and and_1 (and_1_out, D, ~reset, en);  // AND_Gate
  and and_2 (and_2_out, en, ~D);  // AND_Gate
  or or_1 (or_1_out, and_2_out, reset);
  SRlatch srlatch_1 (.S(and_1_out), .R(or_1_out), .Q(Q), .Q1(Q1));
endmodule

module D_Flip_Flop (
  input  D,
  input  clk,
  output Q
);

  wire dlatch_1_q, not_1_out;

  not not_1 (not_1_out, clk);
  DLatch dlatch_1 (.D(D), .en(not_1_out), .Q(dlatch_1_q));  // open: Q1
  DLatch dlatch_2 (.D(dlatch_1_q), .en(clk), .Q(Q));  // open: Q1
endmodule

module D_FlipFlop_SyncReset (
  input  D,
  input  RESET,
  input  CLK,
  output Q
);

  wire and_1_out;

  and and_1 (and_1_out, D, RESET);
  D_Flip_Flop d_flip_flop_1 (.D(and_1_out), .clk(CLK), .Q(Q));
endmodule

module D_FlipFlop_Enable (
  input  D,
  input  en,
  input  clk,
  output Q
);

  wire multiplexer_1_out;

  Multiplexer multiplexer_1 (.in0(Q), .in1(D), .out(multiplexer_1_out), .sel(en));
  D_Flip_Flop d_flip_flop_1 (.D(multiplexer_1_out), .clk(clk), .Q(Q));
endmodule

module T_FlipFlop_From_DFF (
  input  in_1,
  input  in_2,
  output out_3
);

  wire not_1_out;

  D_FlipFlop_SyncReset d_flipflop_syncreset_1 (.D(not_1_out), .RESET(in_1), .CLK(in_2), .Q(out_3));
  not not_1 (not_1_out, out_3);
endmodule

module register_4bit (
  input  D3,
  input  D2,
  input  D1,
  input  D0,
  input  reset,
  input  en,
  input  clk,
  output Q3,
  output Q2,
  output Q1,
  output Q0
);

  wire and_1_out, and_2_out, and_3_out, and_4_out;

  and and_1 (and_1_out, reset, D3);
  D_FlipFlop_Enable d_flipflop_enable_1 (.D(and_1_out), .en(en), .clk(clk), .Q(Q3));
  and and_2 (and_2_out, reset, D2);
  D_FlipFlop_Enable d_flipflop_enable_2 (.D(and_2_out), .en(en), .clk(clk), .Q(Q2));
  and and_3 (and_3_out, reset, D1);
  D_FlipFlop_Enable d_flipflop_enable_3 (.D(and_3_out), .en(en), .clk(clk), .Q(Q1));
  and and_4 (and_4_out, reset, D0);
  D_FlipFlop_Enable d_flipflop_enable_4 (.D(and_4_out), .en(en), .clk(clk), .Q(Q0));
endmodule
