// Logisim project Sum_1to10_Circuit.circ as structural Verilog: 15 circuits, main circuit mainSum_1to10_Circuit
module mainSum_1to10_Circuit (
  input  en,
  input  reset,
  input  fuweien,
  input  reset1,
  input  en1,
  input  fuweien1,
  output [7:0] out_7
);

  wire and_1_out, and_3_out, comparator_1_gt, not_1_out;
  wire [3:0] counter_4bit_1_d1;
  wire [7:0] adder8_complement_1_out_3, and_2_out;
  wire [7:7] clock_1_out;

  Clock clock_1 (.out(clock_1_out[7]));
  and and_1 (and_1_out, comparator_1_gt, en);
  counter_4bit counter_4bit_1 (
    .reset(reset), .en(and_1_out), .fuweien(fuweien), .clk(clock_1_out[7]), .fuweiclk(clock_1_out[7]),
    .d4(counter_4bit_1_d1[3]), .d3(counter_4bit_1_d1[2]), .d2(counter_4bit_1_d1[1]), .d1(counter_4bit_1_d1[0]));
  Comparator comparator_1 (.a(8'hb), .b({4'b0000, counter_4bit_1_d1}), .gt(comparator_1_gt));  // open: eq, lt
  assign and_2_out = out_7 & {8{clock_1_out[7]}};  // AND_Gate and_2, 8 bits wide
  Adder8_Complement adder8_complement_1 (
    .A({4'b0000, counter_4bit_1_d1}), .B(and_2_out), .out_3(adder8_complement_1_out_3));
  not not_1 (not_1_out, clock_1_out[7]);
  and and_3 (and_3_out, en1, comparator_1_gt);
  Register8bit register8bit_1 (
    .c8(adder8_complement_1_out_3[7]), .c7(adder8_complement_1_out_3[6]), .c6(adder8_complement_1_out_3[5]),
    .c5(adder8_complement_1_out_3[4]), .c4(adder8_complement_1_out_3[3]), .c3(adder8_complement_1_out_3[2]),
    .c2(adder8_complement_1_out_3[1]), .c1(adder8_complement_1_out_3[0]), .reset(reset1), .en(and_3_out),
    .fuweien(fuweien1), .clk(not_1_out), .d8(out_7[7]), .d7(out_7[6]), .d6(out_7[5]), .d5(out_7[4]),
    .d4(out_7[3]), .d3(out_7[2]), .d2(out_7[1]), .d1(out_7[0]));
endmodule

module counter_4bit (
  input  reset,
  input  en,
  input  fuweien,
  input  clk,
  input  fuweiclk,
  output d4,
  output d3,
  output d2,
  output d1
);

  wire and_1_out, and_2_out, and_3_out, and_4_out, or_1_out, or_2_out, rca_4bit_1_first, rca_4bit_1_fourth,
       rca_4bit_1_second, rca_4bit_1_third;

  RCA_4bit rca_4bit_1 (
    .a4(d4), .a3(d3), .a2(d2), .a1(d1), .b1(1'b1), .first(rca_4bit_1_first), .second(rca_4bit_1_second),
    .third(rca_4bit_1_third), .fourth(rca_4bit_1_fourth));  // open: b4, b3, b2
  and and_1 (and_1_out, rca_4bit_1_first, reset);
  and and_2 (and_2_out, rca_4bit_1_second, reset);
  and and_3 (and_3_out, rca_4bit_1_third, reset);
  and and_4 (and_4_out, rca_4bit_1_fourth, reset);
  or or_1 (or_1_out, en, fuweien);
  or or_2 (or_2_out, clk, fuweiclk);
  register4bit register4bit_1 (
    .c1(and_1_out), .c2(and_2_out), .c3(and_3_out), .c4(and_4_out), .en(or_1_out), .clk(or_2_out), .d4(d4),
    .d3(d3), .d2(d2), .d1(d1));
  Hex_Digit_Display hex_digit_display_1 (.value({d4, d3, d2, d1}));  // open: dp
endmodule

module SRlatch (
  input  S,
  input  R,
  output Q,
  output Q1
);

  nor nor_1 (Q, R, Q1);
  nor nor_2 (Q1, Q, S);
endmodule

module Dlatch (
  input  D,
  input  we,
  output out_3,
  output out_4
);

  wire and_1_out, and_2_out;

  and and_1 (and_1_out, D, we);
  and and_2 (and_2_out, we, ~D);  // AND_Gate
  SRlatch srlatch_1 (.S(and_1_out), .R(and_2_out), .Q(out_3), .Q1(out_4));
endmodule

module Enabled_DFF (
  input  en,
  input  D,
  input  clk,
  output Q
);

  wire dlatch_1_out_3, multiplexer_1_out, not_1_out;

  Multiplexer multiplexer_1 (.in0(Q), .in1(D), .out(multiplexer_1_out), .sel(en));
  not not_1 (not_1_out, clk);
  Dlatch dlatch_1 (.D(multiplexer_1_out), .we(not_1_out), .out_3(dlatch_1_out_3));  // open: out_4
  Dlatch dlatch_2 (.D(dlatch_1_out_3), .we(clk), .out_3(Q));  // open: out_4
endmodule

module register4bit (
  input  c1,
  input  c2,
  input  c3,
  input  c4,
  input  en,
  input  clk,
  output d4,
  output d3,
  output d2,
  output d1
);

  Enabled_DFF enabled_dff_1 (.en(en), .D(c4), .clk(clk), .Q(d4));
  Enabled_DFF enabled_dff_2 (.en(en), .D(c3), .clk(clk), .Q(d3));
  Enabled_DFF enabled_dff_3 (.en(en), .D(c2), .clk(clk), .Q(d2));
  Hex_Digit_Display hex_digit_display_1 (.value({d4, d3, d2, d1}));  // open: dp
  Enabled_DFF enabled_dff_4 (.en(en), .D(c1), .clk(clk), .Q(d1));
endmodule

module halfadder (
  input  A,
  input  B,
  output S,
  output C
);

  and and_1 (C, A, B);
  xor xor_1 (S, A, B);
endmodule

module fulladder (
  input  A,
  input  B,
  input  Cin,
  output S,
  output Cout
);

  wire halfadder_1_c, halfadder_1_s, halfadder_2_c;

  halfadder halfadder_1 (.A(A), .B(B), .S(halfadder_1_s), .C(halfadder_1_c));
  halfadder halfadder_2 (.A(halfadder_1_s), .B(Cin), .S(S), .C(halfadder_2_c));
  or or_1 (Cout, halfadder_2_c, halfadder_1_c);
endmodule

module RCA_4bit (
  input  a4,
  input  a3,
  input  a2,
  input  a1,
  input  b4,
  input  b3,
  input  b2,
  input  b1,
  output first,
  output second,
  output third,
  output fourth
);

  wire fulladder_1_cout, fulladder_2_cout, fulladder_3_cout, halfadder_1_c, hex_7segment_decoder_1_a1,
       hex_7segment_decoder_1_b1, hex_7segment_decoder_1_c1, hex_7segment_decoder_1_d1,
       hex_7segment_decoder_1_e1, hex_7segment_decoder_1_f1, hex_7segment_decoder_1_g1,
       hex_7segment_decoder_2_a1, hex_7segment_decoder_2_b1, hex_7segment_decoder_2_c1,
       hex_7segment_decoder_2_d1, hex_7segment_decoder_2_e1, hex_7segment_decoder_2_f1,
       hex_7segment_decoder_2_g1, hex_7segment_decoder_3_a1, hex_7segment_decoder_3_b1,
       hex_7segment_decoder_3_c1, hex_7segment_decoder_3_d1, hex_7segment_decoder_3_e1,
       hex_7segment_decoder_3_f1, hex_7segment_decoder_3_g1;

  fulladder fulladder_1 (.A(a4), .B(b4), .Cin(fulladder_2_cout), .S(fourth), .Cout(fulladder_1_cout));
  fulladder fulladder_2 (.A(a3), .B(b3), .Cin(fulladder_3_cout), .S(third), .Cout(fulladder_2_cout));
  fulladder fulladder_3 (.A(a2), .B(b2), .Cin(halfadder_1_c), .S(second), .Cout(fulladder_3_cout));
  halfadder halfadder_1 (.A(a1), .B(b1), .S(first), .C(halfadder_1_c));
  LED led_1 (.in(fulladder_1_cout));
  Hex_7Segment_Decoder hex_7segment_decoder_1 (
    .in_1({fourth, third, second, first}), .a1(hex_7segment_decoder_1_a1), .b1(hex_7segment_decoder_1_b1),
    .c1(hex_7segment_decoder_1_c1), .d1(hex_7segment_decoder_1_d1), .e1(hex_7segment_decoder_1_e1),
    .f1(hex_7segment_decoder_1_f1), .g1(hex_7segment_decoder_1_g1));
  _7_Segment_Display u_7_segment_display_1 (
    .g(hex_7segment_decoder_1_g1), .f(hex_7segment_decoder_1_f1), .a(hex_7segment_decoder_1_a1),
    .b(hex_7segment_decoder_1_b1), .e(hex_7segment_decoder_1_e1), .d(hex_7segment_decoder_1_d1),
    .c(hex_7segment_decoder_1_c1));  // open: dp
  Hex_7Segment_Decoder hex_7segment_decoder_2 (
    .in_1({a4, a3, a2, a1}), .a1(hex_7segment_decoder_2_a1), .b1(hex_7segment_decoder_2_b1),
    .c1(hex_7segment_decoder_2_c1), .d1(hex_7segment_decoder_2_d1), .e1(hex_7segment_decoder_2_e1),
    .f1(hex_7segment_decoder_2_f1), .g1(hex_7segment_decoder_2_g1));
  Hex_7Segment_Decoder hex_7segment_decoder_3 (
    .in_1({b4, b3, b2, b1}), .a1(hex_7segment_decoder_3_a1), .b1(hex_7segment_decoder_3_b1),
    .c1(hex_7segment_decoder_3_c1), .d1(hex_7segment_decoder_3_d1), .e1(hex_7segment_decoder_3_e1),
    .f1(hex_7segment_decoder_3_f1), .g1(hex_7segment_decoder_3_g1));
  _7_Segment_Display u_7_segment_display_2 (
    .g(hex_7segment_decoder_2_g1), .f(hex_7segment_decoder_2_f1), .a(hex_7segment_decoder_2_a1),
    .b(hex_7segment_decoder_2_b1), .e(hex_7segment_decoder_2_e1), .d(hex_7segment_decoder_2_d1),
    .c(hex_7segment_decoder_2_c1));  // open: dp
  _7_Segment_Display u_7_segment_display_3 (
    .g(hex_7segment_decoder_3_g1), .f(hex_7segment_decoder_3_f1), .a(hex_7segment_decoder_3_a1),
    .b(hex_7segment_decoder_3_b1), .e(hex_7segment_decoder_3_e1), .d(hex_7segment_decoder_3_d1),
    .c(hex_7segment_decoder_3_c1));  // open: dp
endmodule

module Adder8_Complement (
  input  [7:0] A,
  input  [7:0] B,
  output [7:0] out_3
);

  wire and_1_out, and_2_out, or_1_out;
  wire [7:0] adder_1_out, adder_2_out, multiplexer_1_out, multiplexer_2_out, not_1_out, not_2_out;

  assign not_1_out = ~B;  // NOT_Gate not_1, 8 bits wide
  assign not_2_out = ~A;  // NOT_Gate not_2, 8 bits wide
  Adder adder_1 (.a({8{1'b1}}), .b(not_1_out), .out(adder_1_out));  // open: cin, cout
  Adder adder_2 (.a({8{1'b1}}), .b(not_2_out), .out(adder_2_out));  // open: cin, cout
  Multiplexer #(.width(8)) multiplexer_1 (.in0(B), .in1(adder_2_out), .out(multiplexer_1_out), .sel(B[7]));
  Multiplexer #(.width(8)) multiplexer_2 (.in0(A), .in1(adder_1_out), .out(multiplexer_2_out), .sel(A[7]));
  Adder adder_3 (.a(multiplexer_1_out), .b(multiplexer_2_out), .out(out_3));  // open: cin, cout
  and and_1 (and_1_out, ~out_3[7], A[7], B[7]);  // AND_Gate
  and and_2 (and_2_out, out_3[7], ~A[7], ~B[7]);  // AND_Gate
  or or_1 (or_1_out, and_1_out, and_2_out);
  LED led_1 (.in(or_1_out));
endmodule

module Hex_7Segment_Decoder (
  input  [3:0] in_1,
  output a1,
  output b1,
  output c1,
  output d1,
  output e1,
  output f1,
  output g1
);

  wire [15:0] decoder4_16_1_out_5;

  decoder4_16 decoder4_16_1 (.in_1(in_1[0]), .in_2(in_1[1]), .in_3(in_1[2]), .Y4(in_1[3]), .out_5(decoder4_16_1_out_5));
  or d (d1, decoder4_16_1_out_5[0], decoder4_16_1_out_5[2], decoder4_16_1_out_5[3], decoder4_16_1_out_5[5], decoder4_16_1_out_5[6], decoder4_16_1_out_5[14], decoder4_16_1_out_5[8], decoder4_16_1_out_5[9], decoder4_16_1_out_5[11], decoder4_16_1_out_5[12], decoder4_16_1_out_5[13]);
  or e (e1, decoder4_16_1_out_5[0], decoder4_16_1_out_5[2], decoder4_16_1_out_5[6], decoder4_16_1_out_5[8], decoder4_16_1_out_5[10], decoder4_16_1_out_5[11], decoder4_16_1_out_5[12], decoder4_16_1_out_5[13], decoder4_16_1_out_5[15], decoder4_16_1_out_5[14]);
  or c (c1, decoder4_16_1_out_5[0], decoder4_16_1_out_5[1], decoder4_16_1_out_5[3], decoder4_16_1_out_5[4], decoder4_16_1_out_5[11], decoder4_16_1_out_5[5], decoder4_16_1_out_5[7], decoder4_16_1_out_5[8], decoder4_16_1_out_5[9], decoder4_16_1_out_5[10], decoder4_16_1_out_5[13], decoder4_16_1_out_5[6]);
  or g (g1, decoder4_16_1_out_5[14], decoder4_16_1_out_5[8], decoder4_16_1_out_5[2], decoder4_16_1_out_5[3], decoder4_16_1_out_5[4], decoder4_16_1_out_5[6], decoder4_16_1_out_5[15], decoder4_16_1_out_5[9], decoder4_16_1_out_5[10], decoder4_16_1_out_5[11], decoder4_16_1_out_5[13], decoder4_16_1_out_5[5]);
  or f (f1, decoder4_16_1_out_5[0], decoder4_16_1_out_5[4], decoder4_16_1_out_5[5], decoder4_16_1_out_5[6], decoder4_16_1_out_5[8], decoder4_16_1_out_5[14], decoder4_16_1_out_5[9], decoder4_16_1_out_5[10], decoder4_16_1_out_5[11], decoder4_16_1_out_5[12], decoder4_16_1_out_5[15]);
  or a (a1, decoder4_16_1_out_5[15], decoder4_16_1_out_5[0], decoder4_16_1_out_5[2], decoder4_16_1_out_5[3], decoder4_16_1_out_5[5], decoder4_16_1_out_5[6], decoder4_16_1_out_5[7], decoder4_16_1_out_5[8], decoder4_16_1_out_5[9], decoder4_16_1_out_5[10], decoder4_16_1_out_5[12], decoder4_16_1_out_5[14]);
  or b (b1, decoder4_16_1_out_5[13], decoder4_16_1_out_5[10], decoder4_16_1_out_5[9], decoder4_16_1_out_5[8], decoder4_16_1_out_5[7], decoder4_16_1_out_5[4], decoder4_16_1_out_5[3], decoder4_16_1_out_5[2], decoder4_16_1_out_5[1], decoder4_16_1_out_5[0]);
endmodule

module Register8bit (
  input  c8,
  input  c7,
  input  c6,
  input  c5,
  input  c4,
  input  c3,
  input  c2,
  input  c1,
  input  reset,
  input  en,
  input  fuweien,
  input  clk,
  output d8,
  output d7,
  output d6,
  output d5,
  output d4,
  output d3,
  output d2,
  output d1
);

  wire and_1_out, and_2_out, and_3_out, and_4_out, and_5_out, and_6_out, and_7_out, and_8_out, or_1_out;

  or or_1 (or_1_out, en, fuweien);
  and and_1 (and_1_out, reset, c8);
  Enabled_DFF enabled_dff_1 (.en(or_1_out), .D(and_1_out), .clk(clk), .Q(d8));
  and and_2 (and_2_out, reset, c7);
  Enabled_DFF enabled_dff_2 (.en(or_1_out), .D(and_2_out), .clk(clk), .Q(d7));
  and and_3 (and_3_out, reset, c6);
  Enabled_DFF enabled_dff_3 (.en(or_1_out), .D(and_3_out), .clk(clk), .Q(d6));
  Hex_Digit_Display hex_digit_display_1 (.value({d8, d7, d6, d5}));  // open: dp
  and and_4 (and_4_out, reset, c5);
  Enabled_DFF enabled_dff_4 (.en(or_1_out), .D(and_4_out), .clk(clk), .Q(d5));
  and and_5 (and_5_out, reset, c4);
  Enabled_DFF enabled_dff_5 (.en(or_1_out), .D(and_5_out), .clk(clk), .Q(d4));
  and and_6 (and_6_out, reset, c3);
  Enabled_DFF enabled_dff_6 (.en(or_1_out), .D(and_6_out), .clk(clk), .Q(d3));
  and and_7 (and_7_out, reset, c2);
  Enabled_DFF enabled_dff_7 (.en(or_1_out), .D(and_7_out), .clk(clk), .Q(d2));
  Hex_Digit_Display hex_digit_display_2 (.value({d4, d3, d2, d1}));  // open: dp
  and and_8 (and_8_out, reset, c1);
  Enabled_DFF enabled_dff_8 (.en(or_1_out), .D(and_8_out), .clk(clk), .Q(d1));
endmodule

module decoder4_16 (
  input  in_1,
  input  in_2,
  input  in_3,
  input  Y4,
  output [15:0] out_5
);

  wire [7:0] decoder3_8_1_out_4, decoder3_8_2_out_4;

  decoder3_8 decoder3_8_1 (.Y0(in_1), .Y1(in_2), .Y2(in_3), .out_4(decoder3_8_1_out_4));
  decoder3_8 decoder3_8_2 (.Y0(in_1), .Y1(in_2), .Y2(in_3), .out_4(decoder3_8_2_out_4));
  assign out_5[7:0] = decoder3_8_1_out_4 & ~{8{Y4}};  // AND_Gate and_1, 8 bits wide
  assign out_5[15:8] = decoder3_8_2_out_4 & {8{Y4}};  // AND_Gate and_2, 8 bits wide
endmodule

module decoder3_8 (
  input  Y0,
  input  Y1,
  input  Y2,
  output [7:0] out_4
);

  wire [3:0] decoder2_4_1_out_3, decoder2_4_2_out_3;

  decoder2_4 decoder2_4_1 (.in_1(Y1), .in_2(Y0), .out_3(decoder2_4_1_out_3));
  decoder2_4 decoder2_4_2 (.in_1(Y1), .in_2(Y0), .out_3(decoder2_4_2_out_3));
  assign out_4[3:0] = decoder2_4_1_out_3 & ~{4{Y2}};  // AND_Gate and_1, 4 bits wide
  assign out_4[7:4] = decoder2_4_2_out_3 & {4{Y2}};  // AND_Gate and_2, 4 bits wide
endmodule

module decoder2_4 (
  input  in_1,
  input  in_2,
  output [3:0] out_3
);

  and and_1 (out_3[3], in_1, in_2);
  and and_2 (out_3[2], in_1, ~in_2);  // AND_Gate
  and and_3 (out_3[1], ~in_1, in_2);  // AND_Gate
  and and_4 (out_3[0], ~in_1, ~in_2);  // AND_Gate
endmodule
