// Logisim project RAM3_8.circ as structural Verilog: 12 circuits, main circuit main
module main (
  input  D7,
  input  D6,
  input  D5,
  input  D4,
  input  D3,
  input  D2,
  input  D1,
  input  D0,
  input  [2:0] adress,
  input  clk,
  input  en,
  input  in_12,
  input  in_13,
  input  in_14,
  output [7:0] out_15
);

  wire and_1_out, and_2_out, and_3_out, and_4_out, and_5_out, and_6_out, and_7_out, and_8_out, and_9_out,
       and_10_out, and_11_out, and_12_out, and_13_out, and_14_out, and_15_out, and_16_out, and_17_out,
       and_18_out, and_19_out, and_20_out, and_21_out, and_22_out, and_23_out, and_24_out, and_25_out,
       and_26_out, and_27_out, and_28_out, and_29_out, and_30_out, and_31_out, and_32_out, and_33_out,
       and_34_out, and_35_out, and_36_out, and_37_out, and_38_out, and_39_out, and_40_out, and_41_out,
       and_42_out, and_43_out, and_44_out, and_45_out, and_46_out, and_47_out, and_48_out, and_49_out,
       and_50_out, and_51_out, and_52_out, and_53_out, and_54_out, and_55_out, and_56_out, and_57_out,
       and_58_out, and_59_out, and_60_out, and_61_out, and_62_out, and_63_out, and_64_out, and_65_out,
       and_66_out, and_67_out, and_68_out, and_69_out, and_70_out, and_71_out, and_72_out, and_73_out,
       and_74_out, and_75_out, and_76_out, and_77_out, and_78_out, and_79_out, and_80_out, and_81_out,
       and_82_out, and_83_out, and_84_out, and_85_out, and_86_out, and_87_out, and_88_out, and_89_out,
       and_90_out, and_91_out, and_92_out, and_93_out, and_94_out, and_95_out, and_96_out, and_97_out,
       and_98_out, and_99_out, and_100_out, and_101_out, and_102_out, and_103_out, and_104_out, and_105_out,
       and_106_out, and_107_out, and_108_out, and_109_out, and_110_out, and_111_out, and_112_out,
       and_113_out, and_114_out, and_115_out, and_116_out, and_117_out, and_118_out, and_119_out,
       and_120_out, and_121_out, and_122_out, and_123_out, and_124_out, and_125_out, and_126_out,
       and_127_out, and_128_out, d_flipflop_enable_1_q, d_flipflop_enable_2_q, d_flipflop_enable_3_q,
       d_flipflop_enable_4_q, d_flipflop_enable_5_q, d_flipflop_enable_6_q, d_flipflop_enable_7_q,
       d_flipflop_enable_8_q, d_flipflop_enable_9_q, d_flipflop_enable_10_q, d_flipflop_enable_11_q,
       d_flipflop_enable_12_q, d_flipflop_enable_13_q, d_flipflop_enable_14_q, d_flipflop_enable_15_q,
       d_flipflop_enable_16_q, d_flipflop_enable_17_q, d_flipflop_enable_18_q, d_flipflop_enable_19_q,
       d_flipflop_enable_20_q, d_flipflop_enable_21_q, d_flipflop_enable_22_q, d_flipflop_enable_23_q,
       d_flipflop_enable_24_q, d_flipflop_enable_25_q, d_flipflop_enable_26_q, d_flipflop_enable_27_q,
       d_flipflop_enable_28_q, d_flipflop_enable_29_q, d_flipflop_enable_30_q, d_flipflop_enable_31_q,
       d_flipflop_enable_32_q, d_flipflop_enable_33_q, d_flipflop_enable_34_q, d_flipflop_enable_35_q,
       d_flipflop_enable_36_q, d_flipflop_enable_37_q, d_flipflop_enable_38_q, d_flipflop_enable_39_q,
       d_flipflop_enable_40_q, d_flipflop_enable_41_q, d_flipflop_enable_42_q, d_flipflop_enable_43_q,
       d_flipflop_enable_44_q, d_flipflop_enable_45_q, d_flipflop_enable_46_q, d_flipflop_enable_47_q,
       d_flipflop_enable_48_q, d_flipflop_enable_49_q, d_flipflop_enable_50_q, d_flipflop_enable_51_q,
       d_flipflop_enable_52_q, d_flipflop_enable_53_q, d_flipflop_enable_54_q, d_flipflop_enable_55_q,
       d_flipflop_enable_56_q, d_flipflop_enable_57_q, d_flipflop_enable_58_q, d_flipflop_enable_59_q,
       d_flipflop_enable_60_q, d_flipflop_enable_61_q, d_flipflop_enable_62_q, d_flipflop_enable_63_q,
       d_flipflop_enable_64_q, decoder3_8_1_y0, decoder3_8_1_y1, decoder3_8_1_y2, decoder3_8_1_y3,
       decoder3_8_1_y4, decoder3_8_1_y5, decoder3_8_1_y6, decoder3_8_1_y7, or_1_out, or_2_out, or_3_out,
       or_4_out, or_5_out, or_6_out, or_7_out, or_8_out;

  decoder3_8 decoder3_8_1 (
    .A(adress[0]), .B(adress[1]), .C(adress[2]), .Y0(decoder3_8_1_y0), .Y1(decoder3_8_1_y1),
    .Y2(decoder3_8_1_y2), .Y3(decoder3_8_1_y3), .Y4(decoder3_8_1_y4), .Y5(decoder3_8_1_y5),
    .Y6(decoder3_8_1_y6), .Y7(decoder3_8_1_y7));
  and and_1 (and_1_out, decoder3_8_1_y0, en);
  and and_2 (and_2_out, decoder3_8_1_y1, en);
  and and_3 (and_3_out, decoder3_8_1_y2, en);
  and and_4 (and_4_out, decoder3_8_1_y3, en);
  and and_5 (and_5_out, decoder3_8_1_y4, en);
  and and_6 (and_6_out, decoder3_8_1_y5, en);
  and and_7 (and_7_out, decoder3_8_1_y6, en);
  and and_8 (and_8_out, decoder3_8_1_y7, en);
  D_FlipFlop_Enable d_flipflop_enable_1 (.D(D7), .en(and_1_out), .clk(clk), .Q(d_flipflop_enable_1_q));
  D_FlipFlop_Enable d_flipflop_enable_2 (.D(D7), .en(and_2_out), .clk(clk), .Q(d_flipflop_enable_2_q));
  D_FlipFlop_Enable d_flipflop_enable_3 (.D(D7), .en(and_3_out), .clk(clk), .Q(d_flipflop_enable_3_q));
  D_FlipFlop_Enable d_flipflop_enable_4 (.D(D7), .en(and_4_out), .clk(clk), .Q(d_flipflop_enable_4_q));
  D_FlipFlop_Enable d_flipflop_enable_5 (.D(D7), .en(and_5_out), .clk(clk), .Q(d_flipflop_enable_5_q));
  D_FlipFlop_Enable d_flipflop_enable_6 (.D(D7), .en(and_6_out), .clk(clk), .Q(d_flipflop_enable_6_q));
  D_FlipFlop_Enable d_flipflop_enable_7 (.D(D7), .en(and_7_out), .clk(clk), .Q(d_flipflop_enable_7_q));
  D_FlipFlop_Enable d_flipflop_enable_8 (.D(D7), .en(and_8_out), .clk(clk), .Q(d_flipflop_enable_8_q));
  and and_9 (and_9_out, decoder3_8_1_y0, d_flipflop_enable_1_q);
  and and_10 (and_10_out, decoder3_8_1_y1, d_flipflop_enable_2_q);
  and and_11 (and_11_out, decoder3_8_1_y2, d_flipflop_enable_3_q);
  and and_12 (and_12_out, decoder3_8_1_y3, d_flipflop_enable_4_q);
  and and_13 (and_13_out, decoder3_8_1_y4, d_flipflop_enable_5_q);
  and and_14 (and_14_out, decoder3_8_1_y5, d_flipflop_enable_6_q);
  and and_15 (and_15_out, decoder3_8_1_y6, d_flipflop_enable_7_q);
  and and_16 (and_16_out, decoder3_8_1_y7, d_flipflop_enable_8_q);
  or or_1 (or_1_out, and_16_out, and_15_out, and_14_out, and_13_out, and_12_out, and_11_out, and_10_out, and_9_out);
  and and_17 (and_17_out, en, decoder3_8_1_y0);
  and and_18 (and_18_out, en, decoder3_8_1_y1);
  and and_19 (and_19_out, en, decoder3_8_1_y2);
  and and_20 (and_20_out, en, decoder3_8_1_y3);
  and and_21 (and_21_out, en, decoder3_8_1_y4);
  and and_22 (and_22_out, en, decoder3_8_1_y5);
  and and_23 (and_23_out, en, decoder3_8_1_y6);
  and and_24 (and_24_out, en, decoder3_8_1_y7);
  and and_25 (and_25_out, decoder3_8_1_y0, d_flipflop_enable_9_q);
  D_FlipFlop_Enable d_flipflop_enable_9 (.D(D6), .en(and_17_out), .clk(clk), .Q(d_flipflop_enable_9_q));
  and and_26 (and_26_out, decoder3_8_1_y1, d_flipflop_enable_10_q);
  D_FlipFlop_Enable d_flipflop_enable_10 (.D(D6), .en(and_18_out), .clk(clk), .Q(d_flipflop_enable_10_q));
  and and_27 (and_27_out, decoder3_8_1_y2, d_flipflop_enable_11_q);
  D_FlipFlop_Enable d_flipflop_enable_11 (.D(D6), .en(and_19_out), .clk(clk), .Q(d_flipflop_enable_11_q));
  and and_28 (and_28_out, decoder3_8_1_y3, d_flipflop_enable_12_q);
  D_FlipFlop_Enable d_flipflop_enable_12 (.D(D6), .en(and_20_out), .clk(clk), .Q(d_flipflop_enable_12_q));
  and and_29 (and_29_out, decoder3_8_1_y4, d_flipflop_enable_13_q);
  D_FlipFlop_Enable d_flipflop_enable_13 (.D(D6), .en(and_21_out), .clk(clk), .Q(d_flipflop_enable_13_q));
  and and_30 (and_30_out, decoder3_8_1_y5, d_flipflop_enable_14_q);
  D_FlipFlop_Enable d_flipflop_enable_14 (.D(D6), .en(and_22_out), .clk(clk), .Q(d_flipflop_enable_14_q));
  and and_31 (and_31_out, decoder3_8_1_y6, d_flipflop_enable_15_q);
  D_FlipFlop_Enable d_flipflop_enable_15 (.D(D6), .en(and_23_out), .clk(clk), .Q(d_flipflop_enable_15_q));
  and and_32 (and_32_out, decoder3_8_1_y7, d_flipflop_enable_16_q);
  D_FlipFlop_Enable d_flipflop_enable_16 (.D(D6), .en(and_24_out), .clk(clk), .Q(d_flipflop_enable_16_q));
  or or_2 (or_2_out, and_32_out, and_31_out, and_30_out, and_29_out, and_28_out, and_27_out, and_26_out, and_25_out);
  and and_33 (and_33_out, decoder3_8_1_y0, en);
  and and_34 (and_34_out, decoder3_8_1_y1, en);
  and and_35 (and_35_out, decoder3_8_1_y2, en);
  and and_36 (and_36_out, decoder3_8_1_y3, en);
  and and_37 (and_37_out, decoder3_8_1_y4, en);
  and and_38 (and_38_out, decoder3_8_1_y5, en);
  and and_39 (and_39_out, decoder3_8_1_y6, en);
  and and_40 (and_40_out, decoder3_8_1_y7, en);
  D_FlipFlop_Enable d_flipflop_enable_17 (.D(D5), .en(and_33_out), .clk(clk), .Q(d_flipflop_enable_17_q));
  D_FlipFlop_Enable d_flipflop_enable_18 (.D(D5), .en(and_34_out), .clk(clk), .Q(d_flipflop_enable_18_q));
  D_FlipFlop_Enable d_flipflop_enable_19 (.D(D5), .en(and_35_out), .clk(clk), .Q(d_flipflop_enable_19_q));
  D_FlipFlop_Enable d_flipflop_enable_20 (.D(D5), .en(and_36_out), .clk(clk), .Q(d_flipflop_enable_20_q));
  D_FlipFlop_Enable d_flipflop_enable_21 (.D(D5), .en(and_37_out), .clk(clk), .Q(d_flipflop_enable_21_q));
  D_FlipFlop_Enable d_flipflop_enable_22 (.D(D5), .en(and_38_out), .clk(clk), .Q(d_flipflop_enable_22_q));
  D_FlipFlop_Enable d_flipflop_enable_23 (.D(D5), .en(and_39_out), .clk(clk), .Q(d_flipflop_enable_23_q));
  D_FlipFlop_Enable d_flipflop_enable_24 (.D(D5), .en(and_40_out), .clk(clk), .Q(d_flipflop_enable_24_q));
  and and_41 (and_41_out, decoder3_8_1_y0, d_flipflop_enable_17_q);
  and and_42 (and_42_out, decoder3_8_1_y1, d_flipflop_enable_18_q);
  and and_43 (and_43_out, decoder3_8_1_y2, d_flipflop_enable_19_q);
  and and_44 (and_44_out, decoder3_8_1_y3, d_flipflop_enable_20_q);
  and and_45 (and_45_out, decoder3_8_1_y4, d_flipflop_enable_21_q);
  and and_46 (and_46_out, decoder3_8_1_y5, d_flipflop_enable_22_q);
  and and_47 (and_47_out, decoder3_8_1_y6, d_flipflop_enable_23_q);
  and and_48 (and_48_out, decoder3_8_1_y7, d_flipflop_enable_24_q);
  or or_3 (or_3_out, and_48_out, and_47_out, and_46_out, and_45_out, and_44_out, and_43_out, and_42_out, and_41_out);
  and and_49 (and_49_out, decoder3_8_1_y0, en);
  and and_50 (and_50_out, decoder3_8_1_y1, en);
  and and_51 (and_51_out, decoder3_8_1_y2, en);
  and and_52 (and_52_out, decoder3_8_1_y3, en);
  and and_53 (and_53_out, decoder3_8_1_y4, en);
  and and_54 (and_54_out, decoder3_8_1_y5, en);
  and and_55 (and_55_out, decoder3_8_1_y6, en);
  and and_56 (and_56_out, decoder3_8_1_y7, en);
  D_FlipFlop_Enable d_flipflop_enable_25 (.D(D4), .en(and_49_out), .clk(clk), .Q(d_flipflop_enable_25_q));
  D_FlipFlop_Enable d_flipflop_enable_26 (.D(D4), .en(and_50_out), .clk(clk), .Q(d_flipflop_enable_26_q));
  D_FlipFlop_Enable d_flipflop_enable_27 (.D(D4), .en(and_51_out), .clk(clk), .Q(d_flipflop_enable_27_q));
  D_FlipFlop_Enable d_flipflop_enable_28 (.D(D4), .en(and_52_out), .clk(clk), .Q(d_flipflop_enable_28_q));
  D_FlipFlop_Enable d_flipflop_enable_29 (.D(D4), .en(and_53_out), .clk(clk), .Q(d_flipflop_enable_29_q));
  D_FlipFlop_Enable d_flipflop_enable_30 (.D(D4), .en(and_54_out), .clk(clk), .Q(d_flipflop_enable_30_q));
  D_FlipFlop_Enable d_flipflop_enable_31 (.D(D4), .en(and_55_out), .clk(clk), .Q(d_flipflop_enable_31_q));
  D_FlipFlop_Enable d_flipflop_enable_32 (.D(D4), .en(and_56_out), .clk(clk), .Q(d_flipflop_enable_32_q));
  and and_57 (and_57_out, decoder3_8_1_y0, d_flipflop_enable_25_q);
  and and_58 (and_58_out, decoder3_8_1_y1, d_flipflop_enable_26_q);
  and and_59 (and_59_out, decoder3_8_1_y2, d_flipflop_enable_27_q);
  and and_60 (and_60_out, decoder3_8_1_y3, d_flipflop_enable_28_q);
  and and_61 (and_61_out, decoder3_8_1_y4, d_flipflop_enable_29_q);
  and and_62 (and_62_out, decoder3_8_1_y5, d_flipflop_enable_30_q);
  and and_63 (and_63_out, decoder3_8_1_y6, d_flipflop_enable_31_q);
  and and_64 (and_64_out, decoder3_8_1_y7, d_flipflop_enable_32_q);
  or or_4 (or_4_out, and_64_out, and_63_out, and_62_out, and_61_out, and_60_out, and_59_out, and_58_out, and_57_out);
  and and_65 (and_65_out, decoder3_8_1_y0, en);
  and and_66 (and_66_out, decoder3_8_1_y1, en);
  and and_67 (and_67_out, decoder3_8_1_y2, en);
  and and_68 (and_68_out, decoder3_8_1_y3, en);
  and and_69 (and_69_out, decoder3_8_1_y4, en);
  and and_70 (and_70_out, decoder3_8_1_y5, en);
  and and_71 (and_71_out, decoder3_8_1_y6, en);
  and and_72 (and_72_out, decoder3_8_1_y7, en);
  D_FlipFlop_Enable d_flipflop_enable_33 (.D(D3), .en(and_65_out), .clk(clk), .Q(d_flipflop_enable_33_q));
  D_FlipFlop_Enable d_flipflop_enable_34 (.D(D3), .en(and_66_out), .clk(clk), .Q(d_flipflop_enable_34_q));
  D_FlipFlop_Enable d_flipflop_enable_35 (.D(D3), .en(and_67_out), .clk(clk), .Q(d_flipflop_enable_35_q));
  D_FlipFlop_Enable d_flipflop_enable_36 (.D(D3), .en(and_68_out), .clk(clk), .Q(d_flipflop_enable_36_q));
  D_FlipFlop_Enable d_flipflop_enable_37 (.D(D3), .en(and_69_out), .clk(clk), .Q(d_flipflop_enable_37_q));
  D_FlipFlop_Enable d_flipflop_enable_38 (.D(D3), .en(and_70_out), .clk(clk), .Q(d_flipflop_enable_38_q));
  D_FlipFlop_Enable d_flipflop_enable_39 (.D(D3), .en(and_71_out), .clk(clk), .Q(d_flipflop_enable_39_q));
  D_FlipFlop_Enable d_flipflop_enable_40 (.D(D3), .en(and_72_out), .clk(clk), .Q(d_flipflop_enable_40_q));
  and and_73 (and_73_out, decoder3_8_1_y0, d_flipflop_enable_33_q);
  and and_74 (and_74_out, decoder3_8_1_y1, d_flipflop_enable_34_q);
  and and_75 (and_75_out, decoder3_8_1_y2, d_flipflop_enable_35_q);
  and and_76 (and_76_out, decoder3_8_1_y3, d_flipflop_enable_36_q);
  and and_77 (and_77_out, decoder3_8_1_y4, d_flipflop_enable_37_q);
  and and_78 (and_78_out, decoder3_8_1_y5, d_flipflop_enable_38_q);
  and and_79 (and_79_out, decoder3_8_1_y6, d_flipflop_enable_39_q);
  and and_80 (and_80_out, decoder3_8_1_y7, d_flipflop_enable_40_q);
  or or_5 (or_5_out, and_80_out, and_79_out, and_78_out, and_77_out, and_76_out, and_75_out, and_74_out, and_73_out);
  and and_81 (and_81_out, decoder3_8_1_y0, en);
  and and_82 (and_82_out, decoder3_8_1_y1, en);
  and and_83 (and_83_out, decoder3_8_1_y2, en);
  and and_84 (and_84_out, decoder3_8_1_y3, en);
  and and_85 (and_85_out, decoder3_8_1_y4, en);
  and and_86 (and_86_out, decoder3_8_1_y5, en);
  and and_87 (and_87_out, decoder3_8_1_y6, en);
  and and_88 (and_88_out, decoder3_8_1_y7, en);
  and and_89 (and_89_out, decoder3_8_1_y0, d_flipflop_enable_41_q);
  D_FlipFlop_Enable d_flipflop_enable_41 (.D(D2), .en(and_81_out), .clk(clk), .Q(d_flipflop_enable_41_q));
  and and_90 (and_90_out, decoder3_8_1_y1, d_flipflop_enable_42_q);
  D_FlipFlop_Enable d_flipflop_enable_42 (.D(D2), .en(and_82_out), .clk(clk), .Q(d_flipflop_enable_42_q));
  and and_91 (and_91_out, decoder3_8_1_y2, d_flipflop_enable_43_q);
  D_FlipFlop_Enable d_flipflop_enable_43 (.D(D2), .en(and_83_out), .clk(clk), .Q(d_flipflop_enable_43_q));
  and and_92 (and_92_out, decoder3_8_1_y3, d_flipflop_enable_44_q);
  D_FlipFlop_Enable d_flipflop_enable_44 (.D(D2), .en(and_84_out), .clk(clk), .Q(d_flipflop_enable_44_q));
  and and_93 (and_93_out, decoder3_8_1_y4, d_flipflop_enable_45_q);
  D_FlipFlop_Enable d_flipflop_enable_45 (.D(D2), .en(and_85_out), .clk(clk), .Q(d_flipflop_enable_45_q));
  and and_94 (and_94_out, decoder3_8_1_y5, d_flipflop_enable_46_q);
  D_FlipFlop_Enable d_flipflop_enable_46 (.D(D2), .en(and_86_out), .clk(clk), .Q(d_flipflop_enable_46_q));
  and and_95 (and_95_out, decoder3_8_1_y6, d_flipflop_enable_47_q);
  D_FlipFlop_Enable d_flipflop_enable_47 (.D(D2), .en(and_87_out), .clk(clk), .Q(d_flipflop_enable_47_q));
  and and_96 (and_96_out, decoder3_8_1_y7, d_flipflop_enable_48_q);
  D_FlipFlop_Enable d_flipflop_enable_48 (.D(D2), .en(and_88_out), .clk(clk), .Q(d_flipflop_enable_48_q));
  or or_6 (or_6_out, and_96_out, and_95_out, and_94_out, and_93_out, and_92_out, and_91_out, and_90_out, and_89_out);
  and and_97 (and_97_out, decoder3_8_1_y0, en);
  and and_98 (and_98_out, decoder3_8_1_y1, en);
  and and_99 (and_99_out, decoder3_8_1_y2, en);
  and and_100 (and_100_out, decoder3_8_1_y3, en);
  and and_101 (and_101_out, decoder3_8_1_y4, en);
  and and_102 (and_102_out, decoder3_8_1_y5, en);
  and and_103 (and_103_out, decoder3_8_1_y6, en);
  and and_104 (and_104_out, decoder3_8_1_y7, en);
  and and_105 (and_105_out, decoder3_8_1_y0, d_flipflop_enable_49_q);
  D_FlipFlop_Enable d_flipflop_enable_49 (.D(D1), .en(and_97_out), .clk(clk), .Q(d_flipflop_enable_49_q));
  and and_106 (and_106_out, decoder3_8_1_y1, d_flipflop_enable_50_q);
  D_FlipFlop_Enable d_flipflop_enable_50 (.D(D1), .en(and_98_out), .clk(clk), .Q(d_flipflop_enable_50_q));
  and and_107 (and_107_out, decoder3_8_1_y2, d_flipflop_enable_51_q);
  D_FlipFlop_Enable d_flipflop_enable_51 (.D(D1), .en(and_99_out), .clk(clk), .Q(d_flipflop_enable_51_q));
  and and_108 (and_108_out, decoder3_8_1_y3, d_flipflop_enable_52_q);
  D_FlipFlop_Enable d_flipflop_enable_52 (.D(D1), .en(and_100_out), .clk(clk), .Q(d_flipflop_enable_52_q));
  and and_109 (and_109_out, decoder3_8_1_y4, d_flipflop_enable_53_q);
  D_FlipFlop_Enable d_flipflop_enable_53 (.D(D1), .en(and_101_out), .clk(clk), .Q(d_flipflop_enable_53_q));
  and and_110 (and_110_out, decoder3_8_1_y5, d_flipflop_enable_54_q);
  D_FlipFlop_Enable d_flipflop_enable_54 (.D(D1), .en(and_102_out), .clk(clk), .Q(d_flipflop_enable_54_q));
  and and_111 (and_111_out, decoder3_8_1_y6, d_flipflop_enable_55_q);
  D_FlipFlop_Enable d_flipflop_enable_55 (.D(D1), .en(and_103_out), .clk(clk), .Q(d_flipflop_enable_55_q));
  and and_112 (and_112_out, decoder3_8_1_y7, d_flipflop_enable_56_q);
  D_FlipFlop_Enable d_flipflop_enable_56 (.D(D1), .en(and_104_out), .clk(clk), .Q(d_flipflop_enable_56_q));
  or or_7 (or_7_out, and_112_out, and_111_out, and_110_out, and_109_out, and_108_out, and_107_out, and_106_out, and_105_out);
  and and_113 (and_113_out, decoder3_8_1_y0, en);
  and and_114 (and_114_out, decoder3_8_1_y1, en);
  and and_115 (and_115_out, decoder3_8_1_y2, en);
  and and_116 (and_116_out, decoder3_8_1_y3, en);
  and and_117 (and_117_out, decoder3_8_1_y4, en);
  and and_118 (and_118_out, decoder3_8_1_y5, en);
  and and_119 (and_119_out, decoder3_8_1_y6, en);
  and and_120 (and_120_out, decoder3_8_1_y7, en);
  D_FlipFlop_Enable d_flipflop_enable_57 (.D(D0), .en(and_113_out), .clk(clk), .Q(d_flipflop_enable_57_q));
  D_FlipFlop_Enable d_flipflop_enable_58 (.en(and_114_out), .clk(clk), .Q(d_flipflop_enable_58_q));  // open: D
  D_FlipFlop_Enable d_flipflop_enable_59 (.D(D0), .en(and_115_out), .clk(clk), .Q(d_flipflop_enable_59_q));
  D_FlipFlop_Enable d_flipflop_enable_60 (.D(D0), .en(and_116_out), .clk(clk), .Q(d_flipflop_enable_60_q));
  D_FlipFlop_Enable d_flipflop_enable_61 (.D(D0), .en(and_117_out), .clk(clk), .Q(d_flipflop_enable_61_q));
  D_FlipFlop_Enable d_flipflop_enable_62 (.D(D0), .en(and_118_out), .clk(clk), .Q(d_flipflop_enable_62_q));
  D_FlipFlop_Enable d_flipflop_enable_63 (.D(D0), .en(and_119_out), .clk(clk), .Q(d_flipflop_enable_63_q));
  D_FlipFlop_Enable d_flipflop_enable_64 (.D(D0), .en(and_120_out), .clk(clk), .Q(d_flipflop_enable_64_q));
  and and_121 (and_121_out, decoder3_8_1_y0, d_flipflop_enable_57_q);
  and and_122 (and_122_out, decoder3_8_1_y1, d_flipflop_enable_58_q);
  and and_123 (and_123_out, decoder3_8_1_y2, d_flipflop_enable_59_q);
  and and_124 (and_124_out, decoder3_8_1_y3, d_flipflop_enable_60_q);
  and and_125 (and_125_out, decoder3_8_1_y4, d_flipflop_enable_61_q);
  and and_126 (and_126_out, decoder3_8_1_y5, d_flipflop_enable_62_q);
  and and_127 (and_127_out, decoder3_8_1_y6, d_flipflop_enable_63_q);
  and and_128 (and_128_out, decoder3_8_1_y7, d_flipflop_enable_64_q);
  or or_8 (or_8_out, and_128_out, and_127_out, and_126_out, and_125_out, and_124_out, and_123_out, and_122_out, and_121_out);
  register_8 register_8_1 (
    .D7(or_1_out), .D6(or_2_out), .D5(or_3_out), .D4(or_4_out), .D3(or_5_out), .D2(or_6_out), .D1(or_7_out),
    .D0(or_8_out), .reset(in_12), .en(in_13), .clk(in_14), .Q7(out_15[7]), .Q6(out_15[6]), .Q5(out_15[5]),
    .Q4(out_15[4]), .Q3(out_15[3]), .Q2(out_15[2]), .Q1(out_15[1]), .Q0(out_15[0]));
endmodule

module ROM3_8 (
  input  [2:0] adress,
  input  in_2,
  input  in_3,
  input  in_4,
  input  in_5,
  input  in_6,
  input  in_7,
  input  in_8,
  input  in_9,
  input  in_10,
  input  in_11,
  input  in_12,
  input  in_13,
  input  in_14,
  input  in_15,
  input  in_16,
  input  in_17,
  input  in_18,
  input  in_19,
  input  in_20,
  input  in_21,
  input  in_22,
  input  in_23,
  input  in_24,
  input  in_25,
  input  in_26,
  input  in_27,
  input  in_28,
  input  in_29,
  input  in_30,
  input  in_31,
  input  in_32,
  input  in_33,
  input  in_34,
  input  in_35,
  input  in_36,
  input  in_37,
  input  in_38,
  input  in_39,
  input  in_40,
  input  in_41,
  input  in_42,
  input  in_43,
  input  in_44,
  input  in_45,
  input  in_46,
  input  in_47,
  input  in_48,
  input  in_49,
  input  in_50,
  input  in_51,
  input  in_52,
  input  in_53,
  input  in_54,
  input  in_55,
  input  in_56,
  input  in_57,
  input  in_58,
  input  in_59,
  input  in_60,
  input  in_61,
  input  in_62,
  input  in_63,
  input  in_64,
  input  in_65,
  input  in_66,
  input  in_67,
  input  in_68,
  output [7:0] out_69
);

  wire and_1_out, and_2_out, and_3_out, and_4_out, and_5_out, and_6_out, and_7_out, and_8_out, and_9_out,
       and_10_out, and_11_out, and_12_out, and_13_out, and_14_out, and_15_out, and_16_out, and_17_out,
       and_18_out, and_19_out, and_20_out, and_21_out, and_22_out, and_23_out, and_24_out, and_25_out,
       and_26_out, and_27_out, and_28_out, and_29_out, and_30_out, and_31_out, and_32_out, and_33_out,
       and_34_out, and_35_out, and_36_out, and_37_out, and_38_out, and_39_out, and_40_out, and_41_out,
       and_42_out, and_43_out, and_44_out, and_45_out, and_46_out, and_47_out, and_48_out, and_49_out,
       and_50_out, and_51_out, and_52_out, and_53_out, and_54_out, and_55_out, and_56_out, and_57_out,
       and_58_out, and_59_out, and_60_out, and_61_out, and_62_out, and_63_out, and_64_out, decoder3_8_1_y0,
       decoder3_8_1_y1, decoder3_8_1_y2, decoder3_8_1_y3, decoder3_8_1_y4, decoder3_8_1_y5, decoder3_8_1_y6,
       decoder3_8_1_y7, or_1_out, or_2_out, or_3_out, or_4_out, or_5_out, or_6_out, or_7_out, or_8_out;

  decoder3_8 decoder3_8_1 (
    .A(adress[0]), .B(adress[1]), .C(adress[2]), .Y0(decoder3_8_1_y0), .Y1(decoder3_8_1_y1),
    .Y2(decoder3_8_1_y2), .Y3(decoder3_8_1_y3), .Y4(decoder3_8_1_y4), .Y5(decoder3_8_1_y5),
    .Y6(decoder3_8_1_y6), .Y7(decoder3_8_1_y7));
  and and_1 (and_1_out, decoder3_8_1_y0, in_2);
  and and_2 (and_2_out, decoder3_8_1_y1, in_10);
  and and_3 (and_3_out, decoder3_8_1_y2, in_18);
  and and_4 (and_4_out, decoder3_8_1_y3, in_26);
  and and_5 (and_5_out, decoder3_8_1_y4, in_34);
  and and_6 (and_6_out, decoder3_8_1_y5, in_42);
  and and_7 (and_7_out, decoder3_8_1_y6, in_50);
  and and_8 (and_8_out, decoder3_8_1_y7, in_58);
  or or_1 (or_1_out, and_8_out, and_7_out, and_6_out, and_5_out, and_4_out, and_3_out, and_2_out, and_1_out);
  and and_9 (and_9_out, decoder3_8_1_y0, in_3);
  and and_10 (and_10_out, decoder3_8_1_y1, in_11);
  and and_11 (and_11_out, decoder3_8_1_y2, in_19);
  and and_12 (and_12_out, decoder3_8_1_y3, in_27);
  and and_13 (and_13_out, decoder3_8_1_y4, in_35);
  and and_14 (and_14_out, decoder3_8_1_y5, in_43);
  and and_15 (and_15_out, decoder3_8_1_y6, in_51);
  and and_16 (and_16_out, decoder3_8_1_y7, in_59);
  or or_2 (or_2_out, and_16_out, and_15_out, and_14_out, and_13_out, and_12_out, and_11_out, and_10_out, and_9_out);
  and and_17 (and_17_out, decoder3_8_1_y0, in_4);
  and and_18 (and_18_out, decoder3_8_1_y1, in_12);
  and and_19 (and_19_out, decoder3_8_1_y2, in_20);
  and and_20 (and_20_out, decoder3_8_1_y3, in_28);
  and and_21 (and_21_out, decoder3_8_1_y4, in_36);
  and and_22 (and_22_out, decoder3_8_1_y5, in_44);
  and and_23 (and_23_out, decoder3_8_1_y6, in_52);
  and and_24 (and_24_out, decoder3_8_1_y7, in_60);
  or or_3 (or_3_out, and_24_out, and_23_out, and_22_out, and_21_out, and_20_out, and_19_out, and_18_out, and_17_out);
  and and_25 (and_25_out, decoder3_8_1_y0, in_5);
  and and_26 (and_26_out, decoder3_8_1_y1, in_13);
  and and_27 (and_27_out, decoder3_8_1_y2, in_21);
  and and_28 (and_28_out, decoder3_8_1_y3, in_29);
  and and_29 (and_29_out, decoder3_8_1_y4, in_37);
  and and_30 (and_30_out, decoder3_8_1_y5, in_45);
  and and_31 (and_31_out, decoder3_8_1_y6, in_53);
  and and_32 (and_32_out, decoder3_8_1_y7, in_61);
  or or_4 (or_4_out, and_32_out, and_31_out, and_30_out, and_29_out, and_28_out, and_27_out, and_26_out, and_25_out);
  and and_33 (and_33_out, decoder3_8_1_y0, in_6);
  and and_34 (and_34_out, decoder3_8_1_y1, in_14);
  and and_35 (and_35_out, decoder3_8_1_y2, in_22);
  and and_36 (and_36_out, decoder3_8_1_y3, in_30);
  and and_37 (and_37_out, decoder3_8_1_y4, in_38);
  and and_38 (and_38_out, decoder3_8_1_y5, in_46);
  and and_39 (and_39_out, decoder3_8_1_y6, in_54);
  and and_40 (and_40_out, decoder3_8_1_y7, in_62);
  or or_5 (or_5_out, and_40_out, and_39_out, and_38_out, and_37_out, and_36_out, and_35_out, and_34_out, and_33_out);
  and and_41 (and_41_out, decoder3_8_1_y0, in_7);
  and and_42 (and_42_out, decoder3_8_1_y1, in_15);
  and and_43 (and_43_out, decoder3_8_1_y2, in_23);
  and and_44 (and_44_out, decoder3_8_1_y3, in_31);
  and and_45 (and_45_out, decoder3_8_1_y4, in_39);
  and and_46 (and_46_out, decoder3_8_1_y5, in_47);
  and and_47 (and_47_out, decoder3_8_1_y6, in_55);
  and and_48 (and_48_out, decoder3_8_1_y7, in_63);
  or or_6 (or_6_out, and_48_out, and_47_out, and_46_out, and_45_out, and_44_out, and_43_out, and_42_out, and_41_out);
  and and_49 (and_49_out, decoder3_8_1_y0, in_8);
  and and_50 (and_50_out, decoder3_8_1_y1, in_16);
  and and_51 (and_51_out, decoder3_8_1_y2, in_24);
  and and_52 (and_52_out, decoder3_8_1_y3, in_32);
  and and_53 (and_53_out, decoder3_8_1_y4, in_40);
  and and_54 (and_54_out, decoder3_8_1_y5, in_48);
  and and_55 (and_55_out, decoder3_8_1_y6, in_56);
  and and_56 (and_56_out, decoder3_8_1_y7, in_64);
  or or_7 (or_7_out, and_56_out, and_55_out, and_54_out, and_53_out, and_52_out, and_51_out, and_50_out, and_49_out);
  and and_57 (and_57_out, decoder3_8_1_y0, in_9);
  and and_58 (and_58_out, decoder3_8_1_y1, in_17);
  and and_59 (and_59_out, decoder3_8_1_y2, in_25);
  and and_60 (and_60_out, decoder3_8_1_y3, in_33);
  and and_61 (and_61_out, decoder3_8_1_y4, in_41);
  and and_62 (and_62_out, decoder3_8_1_y5, in_49);
  and and_63 (and_63_out, decoder3_8_1_y6, in_57);
  and and_64 (and_64_out, decoder3_8_1_y7, in_65);
  or or_8 (or_8_out, and_64_out, and_63_out, and_62_out, and_61_out, and_60_out, and_59_out, and_58_out, and_57_out);
  register_8 register_8_1 (
    .D7(or_1_out), .D6(or_2_out), .D5(or_3_out), .D4(or_4_out), .D3(or_5_out), .D2(or_6_out), .D1(or_7_out),
    .D0(or_8_out), .reset(in_66), .en(in_67), .clk(in_68), .Q7(out_69[7]), .Q6(out_69[6]), .Q5(out_69[5]),
    .Q4(out_69[4]), .Q3(out_69[3]), .Q2(out_69[2]), .Q1(out_69[1]), .Q0(out_69[0]));
endmodule

module decoder2_4 (
  input  A,
  input  B,
  output [3:0] out_3
);

  and and_1 (out_3[0], ~A, ~B);  // AND_Gate
  and and_2 (out_3[1], A, ~B);  // AND_Gate
  and and_3 (out_3[2], ~A, B);  // AND_Gate
  and and_4 (out_3[3], A, B);
endmodule

module decoder3_8 (
  input  A,
  input  B,
  input  C,
  output Y0,
  output Y1,
  output Y2,
  output Y3,
  output Y4,
  output Y5,
  output Y6,
  output Y7
);

  wire [3:0] decoder2_4_1_out_3, decoder2_4_2_out_3;

  decoder2_4 decoder2_4_1 (.A(A), .B(B), .out_3(decoder2_4_1_out_3));
  decoder2_4 decoder2_4_2 (.A(A), .B(B), .out_3(decoder2_4_2_out_3));
  assign {Y3, Y2, Y1, Y0} = decoder2_4_1_out_3 & ~{4{C}};  // AND_Gate and_1, 4 bits wide
  assign {Y7, Y6, Y5, Y4} = decoder2_4_2_out_3 & {4{C}};  // AND_Gate and_2, 4 bits wide
endmodule

module SRlatch (
  input  S,
  input  R,
  output Q,
  output Q1
);

  nor nor_1 (Q, R, Q1);
  nor nor_2 (Q1, Q, S);
endmodule

module DLatch (
  input  D,
  input  en,
  output Q,
  output Q1
);

  wire and_1_out, and_2_out;

  and and_1 (and_1_out, D, en);
  and and_2 (and_2_out, en, ~D);  // AND_Gate
  SRlatch srlatch_1 (.S(and_1_out), .R(and_2_out), .Q(Q), .Q1(Q1));
endmodule

module Toggling_D_Latch_Reset (
  input  D,
  input  en,
  input  reset,
  output Q,
  output Q1
);

  wire and_1_out, and_2_out, or_1_out;

  and and_1 (and_1_out, D, ~reset, en);  // AND_Gate
  and and_2 (and_2_out, en, ~D);  // AND_Gate
  or or_1 (or_1_out, and_2_out, reset);
  SRlatch srlatch_1 (.S(and_1_out), .R(or_1_out), .Q(Q), .Q1(Q1));
endmodule

module D_Flip_Flop (
  input  D,
  input  clk,
  output Q
);

  wire dlatch_1_q, not_1_out;

  not not_1 (not_1_out, clk);
  DLatch dlatch_1 (.D(D), .en(not_1_out), .Q(dlatch_1_q));  // open: Q1
  DLatch dlatch_2 (.D(dlatch_1_q), .en(clk), .Q(Q));  // open: Q1
endmodule

module D_FlipFlop_SyncReset (
  input  D,
  input  RESET,
  input  CLK,
  output Q
);

  wire and_1_out;

  and and_1 (and_1_out, D, RESET);
  D_Flip_Flop d_flip_flop_1 (.D(and_1_out), .clk(CLK), .Q(Q));
endmodule

module D_FlipFlop_Enable (
  input  D,
  input  en,
  input  clk,
  output Q
);

  wire multiplexer_1_out;

  Multiplexer multiplexer_1 (.in0(Q), .in1(D), .out(multiplexer_1_out), .sel(en));
  D_Flip_Flop d_flip_flop_1 (.D(multiplexer_1_out), .clk(clk), .Q(Q));
endmodule

module T_FlipFlop_From_DFF (
  input  in_1,
  input  in_2,
  output out_3
);

  wire not_1_out;

  D_FlipFlop_SyncReset d_flipflop_syncreset_1 (.D(not_1_out), .RESET(in_1), .CLK(in_2), .Q(out_3));
  not not_1 (not_1_out, out_3);
endmodule

module register_8 (
  input  D7,
  input  D6,
  input  D5,
  input  D4,
  input  D3,
  input  D2,
  input  D1,
  input  D0,
  input  reset,
  input  en,
  input  clk,
  output Q7,
  output Q6,
  output Q5,
  output Q4,
  output Q3,
  output Q2,
  output Q1,
  output Q0
);

  wire and_1_out, and_2_out, and_3_out, and_4_out, and_5_out, and_6_out, and_7_out, and_8_out;

  and and_1 (and_1_out, reset, D7);
  D_FlipFlop_Enable d_flipflop_enable_1 (.D(and_1_out), .en(en), .clk(clk), .Q(Q7));
  and and_2 (and_2_out, reset, D6);
  D_FlipFlop_Enable d_flipflop_enable_2 (.D(and_2_out), .en(en), .clk(clk), .Q(Q6));
  and and_3 (and_3_out, reset, D5);
  D_FlipFlop_Enable d_flipflop_enable_3 (.D(and_3_out), .en(en), .clk(clk), .Q(Q5));
  and and_4 (and_4_out, reset, D4);
  D_FlipFlop_Enable d_flipflop_enable_4 (.D(and_4_out), .en(en), .clk(clk), .Q(Q4));
  and and_5 (and_5_out, reset, D3);
  D_FlipFlop_Enable d_flipflop_enable_5 (.D(and_5_out), .en(en), .clk(clk), .Q(Q3));
  and and_6 (and_6_out, reset, D2);
  D_FlipFlop_Enable d_flipflop_enable_6 (.D(and_6_out), .en(en), .clk(clk), .Q(Q2));
  and and_7 (and_7_out, reset, D1);
  D_FlipFlop_Enable d_flipflop_enable_7 (.D(and_7_out), .en(en), .clk(clk), .Q(Q1));
  and and_8 (and_8_out, reset, D0);
  D_FlipFlop_Enable d_flipflop_enable_8 (.D(and_8_out), .en(en), .clk(clk), .Q(Q0));
endmodule
