// Logisim project ROM_8_8.circ as structural Verilog: 11 circuits, main circuit ROM3_8
module ROM3_8 (
  input  [2:0] adress,
  input  in_2,
  input  in_3,
  input  in_4,
  output [7:0] out_5
);

  wire and_1_out, and_2_out, and_3_out, and_4_out, and_5_out, and_6_out, and_7_out, and_8_out, and_9_out,
       and_10_out, and_11_out, and_12_out, and_13_out, and_14_out, and_15_out, and_16_out, and_17_out,
       and_18_out, and_19_out, and_20_out, and_21_out, and_22_out, and_23_out, and_24_out, and_25_out,
       and_26_out, and_27_out, and_28_out, and_29_out, and_30_out, and_31_out, and_32_out, and_33_out,
       and_34_out, and_35_out, and_36_out, and_37_out, and_38_out, and_39_out, and_40_out, and_41_out,
       and_42_out, and_43_out, and_44_out, and_45_out, and_46_out, and_47_out, and_48_out, and_49_out,
       and_50_out, and_51_out, and_52_out, and_53_out, and_54_out, and_55_out, and_56_out, and_57_out,
       and_58_out, and_59_out, and_60_out, and_61_out, and_62_out, and_63_out, and_64_out, decoder3_8_1_y0,
       decoder3_8_1_y1, decoder3_8_1_y2, decoder3_8_1_y3, decoder3_8_1_y4, decoder3_8_1_y5, decoder3_8_1_y6,
       decoder3_8_1_y7, or_1_out, or_2_out, or_3_out, or_4_out, or_5_out, or_6_out, or_7_out, or_8_out;

  decoder3_8 decoder3_8_1 (
    .A(adress[0]), .B(adress[1]), .C(adress[2]), .Y0(decoder3_8_1_y0), .Y1(decoder3_8_1_y1),
    .Y2(decoder3_8_1_y2), .Y3(decoder3_8_1_y3), .Y4(decoder3_8_1_y4), .Y5(decoder3_8_1_y5),
    .Y6(decoder3_8_1_y6), .Y7(decoder3_8_1_y7));
  and and_1 (and_1_out, decoder3_8_1_y0, 1'b1);
  and and_2 (and_2_out, decoder3_8_1_y1, 1'b1);
  and and_3 (and_3_out, decoder3_8_1_y2, 1'b1);
  and and_4 (and_4_out, decoder3_8_1_y3, 1'b1);
  and and_5 (and_5_out, decoder3_8_1_y4, 1'b0);
  and and_6 (and_6_out, decoder3_8_1_y5, 1'b0);
  and and_7 (and_7_out, decoder3_8_1_y6, 1'b1);
  and and_8 (and_8_out, decoder3_8_1_y7, 1'b1);
  or or_1 (or_1_out, and_8_out, and_7_out, and_6_out, and_5_out, and_4_out, and_3_out, and_2_out, and_1_out);
  and and_9 (and_9_out, decoder3_8_1_y0, 1'b0);
  and and_10 (and_10_out, decoder3_8_1_y1, 1'b0);
  and and_11 (and_11_out, decoder3_8_1_y2, 1'b0);
  and and_12 (and_12_out, decoder3_8_1_y3, 1'b0);
  and and_13 (and_13_out, decoder3_8_1_y4, 1'b0);
  and and_14 (and_14_out, decoder3_8_1_y5, 1'b0);
  and and_15 (and_15_out, decoder3_8_1_y6, 1'b1);
  and and_16 (and_16_out, decoder3_8_1_y7, 1'b1);
  or or_2 (or_2_out, and_16_out, and_15_out, and_14_out, and_13_out, and_12_out, and_11_out, and_10_out, and_9_out);
  and and_17 (and_17_out, decoder3_8_1_y0, 1'b0);
  and and_18 (and_18_out, decoder3_8_1_y1, 1'b0);
  and and_19 (and_19_out, decoder3_8_1_y2, 1'b1);
  and and_20 (and_20_out, decoder3_8_1_y3, 1'b1);
  and and_21 (and_21_out, decoder3_8_1_y4, 1'b0);
  and and_22 (and_22_out, decoder3_8_1_y5, 1'b1);
  and and_23 (and_23_out, decoder3_8_1_y6, 1'b0);
  and and_24 (and_24_out, decoder3_8_1_y7, 1'b0);
  or or_3 (or_3_out, and_24_out, and_23_out, and_22_out, and_21_out, and_20_out, and_19_out, and_18_out, and_17_out);
  and and_25 (and_25_out, decoder3_8_1_y0, 1'b0);
  and and_26 (and_26_out, decoder3_8_1_y1, 1'b1);
  and and_27 (and_27_out, decoder3_8_1_y2, 1'b0);
  and and_28 (and_28_out, decoder3_8_1_y3, 1'b1);
  and and_29 (and_29_out, decoder3_8_1_y4, 1'b1);
  and and_30 (and_30_out, decoder3_8_1_y5, 1'b0);
  and and_31 (and_31_out, decoder3_8_1_y6, 1'b1);
  and and_32 (and_32_out, decoder3_8_1_y7, 1'b1);
  or or_4 (or_4_out, and_32_out, and_31_out, and_30_out, and_29_out, and_28_out, and_27_out, and_26_out, and_25_out);
  and and_33 (and_33_out, decoder3_8_1_y0, 1'b1);
  and and_34 (and_34_out, decoder3_8_1_y1, 1'b0);
  and and_35 (and_35_out, decoder3_8_1_y2, 1'b0);
  and and_36 (and_36_out, decoder3_8_1_y3, 1'b0);
  and and_37 (and_37_out, decoder3_8_1_y4, 1'b0);
  and and_38 (and_38_out, decoder3_8_1_y5, 1'b1);
  and and_39 (and_39_out, decoder3_8_1_y6, 1'b0);
  and and_40 (and_40_out, decoder3_8_1_y7, 1'b1);
  or or_5 (or_5_out, and_40_out, and_39_out, and_38_out, and_37_out, and_36_out, and_35_out, and_34_out, and_33_out);
  and and_41 (and_41_out, decoder3_8_1_y0, 1'b0);
  and and_42 (and_42_out, decoder3_8_1_y1, 1'b0);
  and and_43 (and_43_out, decoder3_8_1_y2, 1'b0);
  and and_44 (and_44_out, decoder3_8_1_y3, 1'b0);
  and and_45 (and_45_out, decoder3_8_1_y4, 1'b1);
  and and_46 (and_46_out, decoder3_8_1_y5, 1'b0);
  and and_47 (and_47_out, decoder3_8_1_y6, 1'b0);
  and and_48 (and_48_out, decoder3_8_1_y7, 1'b1);
  or or_6 (or_6_out, and_48_out, and_47_out, and_46_out, and_45_out, and_44_out, and_43_out, and_42_out, and_41_out);
  and and_49 (and_49_out, decoder3_8_1_y0, 1'b1);
  and and_50 (and_50_out, decoder3_8_1_y1, 1'b0);
  and and_51 (and_51_out, decoder3_8_1_y2, 1'b0);
  and and_52 (and_52_out, decoder3_8_1_y3, 1'b0);
  and and_53 (and_53_out, decoder3_8_1_y4, 1'b1);
  and and_54 (and_54_out, decoder3_8_1_y5, 1'b0);
  and and_55 (and_55_out, decoder3_8_1_y6, 1'b0);
  and and_56 (and_56_out, decoder3_8_1_y7, 1'b1);
  or or_7 (or_7_out, and_56_out, and_55_out, and_54_out, and_53_out, and_52_out, and_51_out, and_50_out, and_49_out);
  and and_57 (and_57_out, decoder3_8_1_y0, 1'b0);
  and and_58 (and_58_out, decoder3_8_1_y1, 1'b0);
  and and_59 (and_59_out, decoder3_8_1_y2, 1'b0);
  and and_60 (and_60_out, decoder3_8_1_y3, 1'b1);
  and and_61 (and_61_out, decoder3_8_1_y4, 1'b1);
  and and_62 (and_62_out, decoder3_8_1_y5, 1'b1);
  and and_63 (and_63_out, decoder3_8_1_y6, 1'b1);
  and and_64 (and_64_out, decoder3_8_1_y7, 1'b1);
  or or_8 (or_8_out, and_64_out, and_63_out, and_62_out, and_61_out, and_60_out, and_59_out, and_58_out, and_57_out);
  register_8 register_8_1 (
    .D7(or_1_out), .D6(or_2_out), .D5(or_3_out), .D4(or_4_out), .D3(or_5_out), .D2(or_6_out), .D1(or_7_out),
    .D0(or_8_out), .reset(in_2), .en(in_3), .clk(in_4), .Q7(out_5[7]), .Q6(out_5[6]), .Q5(out_5[5]),
    .Q4(out_5[4]), .Q3(out_5[3]), .Q2(out_5[2]), .Q1(out_5[1]), .Q0(out_5[0]));
endmodule

module decoder2_4 (
  input  A,
  input  B,
  output [3:0] out_3
);

  and and_1 (out_3[0], ~A, ~B);  // AND_Gate
  and and_2 (out_3[1], A, ~B);  // AND_Gate
  and and_3 (out_3[2], ~A, B);  // AND_Gate
  and and_4 (out_3[3], A, B);
endmodule

module decoder3_8 (
  input  A,
  input  B,
  input  C,
  output Y0,
  output Y1,
  output Y2,
  output Y3,
  output Y4,
  output Y5,
  output Y6,
  output Y7
);

  wire [3:0] decoder2_4_1_out_3, decoder2_4_2_out_3;

  decoder2_4 decoder2_4_1 (.A(A), .B(B), .out_3(decoder2_4_1_out_3));
  decoder2_4 decoder2_4_2 (.A(A), .B(B), .out_3(decoder2_4_2_out_3));
  assign {Y3, Y2, Y1, Y0} = decoder2_4_1_out_3 & ~{4{C}};  // AND_Gate and_1, 4 bits wide
  assign {Y7, Y6, Y5, Y4} = decoder2_4_2_out_3 & {4{C}};  // AND_Gate and_2, 4 bits wide
endmodule

module SRlatch (
  input  S,
  input  R,
  output Q,
  output Q1
);

  nor nor_1 (Q, R, Q1);
  nor nor_2 (Q1, Q, S);
endmodule

module DLatch (
  input  D,
  input  en,
  output Q,
  output Q1
);

  wire and_1_out, and_2_out;

  and and_1 (and_1_out, D, en);
  and and_2 (and_2_out, en, ~D);  // AND_Gate
  SRlatch srlatch_1 (.S(and_1_out), .R(and_2_out), .Q(Q), .Q1(Q1));
endmodule

module Toggling_D_Latch_Reset (
  input  D,
  input  en,
  input  reset,
  output Q,
  output Q1
);

  wire and_1_out, and_2_out, or_1_out;

  and and_1 (and_1_out, D, ~reset, en);  // AND_Gate
  and and_2 (and_2_out, en, ~D);  // AND_Gate
  or or_1 (or_1_out, and_2_out, reset);
  SRlatch srlatch_1 (.S(and_1_out), .R(or_1_out), .Q(Q), .Q1(Q1));
endmodule

module D_Flip_Flop (
  input  D,
  input  clk,
  output Q
);

  wire dlatch_1_q, not_1_out;

  not not_1 (not_1_out, clk);
  DLatch dlatch_1 (.D(D), .en(not_1_out), .Q(dlatch_1_q));  // open: Q1
  DLatch dlatch_2 (.D(dlatch_1_q), .en(clk), .Q(Q));  // open: Q1
endmodule

module D_FlipFlop_SyncReset (
  input  D,
  input  RESET,
  input  CLK,
  output Q
);

  wire and_1_out;

  and and_1 (and_1_out, D, RESET);
  D_Flip_Flop d_flip_flop_1 (.D(and_1_out), .clk(CLK), .Q(Q));
endmodule

module D_FlipFlop_Enable (
  input  D,
  input  en,
  input  clk,
  output Q
);

  wire multiplexer_1_out;

  Multiplexer multiplexer_1 (.in0(Q), .in1(D), .out(multiplexer_1_out), .sel(en));
  D_Flip_Flop d_flip_flop_1 (.D(multiplexer_1_out), .clk(clk), .Q(Q));
endmodule

module T_FlipFlop_From_DFF (
  input  in_1,
  input  in_2,
  output out_3
);

  wire not_1_out;

  D_FlipFlop_SyncReset d_flipflop_syncreset_1 (.D(not_1_out), .RESET(in_1), .CLK(in_2), .Q(out_3));
  not not_1 (not_1_out, out_3);
endmodule

module register_8 (
  input  D7,
  input  D6,
  input  D5,
  input  D4,
  input  D3,
  input  D2,
  input  D1,
  input  D0,
  input  reset,
  input  en,
  input  clk,
  output Q7,
  output Q6,
  output Q5,
  output Q4,
  output Q3,
  output Q2,
  output Q1,
  output Q0
);

  wire and_1_out, and_2_out, and_3_out, and_4_out, and_5_out, and_6_out, and_7_out, and_8_out;

  and and_1 (and_1_out, reset, D7);
  D_FlipFlop_Enable d_flipflop_enable_1 (.D(and_1_out), .en(en), .clk(clk), .Q(Q7));
  and and_2 (and_2_out, reset, D6);
  D_FlipFlop_Enable d_flipflop_enable_2 (.D(and_2_out), .en(en), .clk(clk), .Q(Q6));
  and and_3 (and_3_out, reset, D5);
  D_FlipFlop_Enable d_flipflop_enable_3 (.D(and_3_out), .en(en), .clk(clk), .Q(Q5));
  and and_4 (and_4_out, reset, D4);
  D_FlipFlop_Enable d_flipflop_enable_4 (.D(and_4_out), .en(en), .clk(clk), .Q(Q4));
  and and_5 (and_5_out, reset, D3);
  D_FlipFlop_Enable d_flipflop_enable_5 (.D(and_5_out), .en(en), .clk(clk), .Q(Q3));
  and and_6 (and_6_out, reset, D2);
  D_FlipFlop_Enable d_flipflop_enable_6 (.D(and_6_out), .en(en), .clk(clk), .Q(Q2));
  and and_7 (and_7_out, reset, D1);
  D_FlipFlop_Enable d_flipflop_enable_7 (.D(and_7_out), .en(en), .clk(clk), .Q(Q1));
  and and_8 (and_8_out, reset, D0);
  D_FlipFlop_Enable d_flipflop_enable_8 (.D(and_8_out), .en(en), .clk(clk), .Q(Q0));
endmodule
