// Logisim project Scpu_only_li.circ as structural Verilog: 21 circuits, main circuit sCPU_li_only
module sCPU_li_only (
  input  in_1,
  input  in_2,
  input  in_3,
  input  in_4,
  output [3:0] imm,
  output [7:0] out_6,
  output [1:0] rd,
  output [1:0] opcode
);

  wire clock_1_out;
  wire [1:0] counter_4bit_1_d1;

  Clock clock_1 (.out(clock_1_out));
  counter_4bit counter_4bit_1 (
    .reset(in_1), .en(in_2), .fuweien(in_3), .clk(clock_1_out), .fuweiclk(in_4), .d2(counter_4bit_1_d1[1]),
    .d1(counter_4bit_1_d1[0]));  // open: d4, d3
  ROM_8_8 rom_8_8_1 (.in_1(counter_4bit_1_d1), .clk(clock_1_out), .out_3({opcode, rd, imm}));
  RAM_4_8 ram_4_8_1 (
    .D7(1'b0), .D6(1'b0), .D5(1'b0), .D4(1'b0), .D3(imm[3]), .D2(imm[2]), .D1(imm[1]), .D0(imm[0]),
    .address(rd), .en(in_2), .clk(clock_1_out), .a7(out_6[7]), .a6(out_6[6]), .a5(out_6[5]), .a4(out_6[4]),
    .a3(out_6[3]), .a2(out_6[2]), .a1(out_6[1]), .a0(out_6[0]));
endmodule

module RAM_4_8 (
  input  D7,
  input  D6,
  input  D5,
  input  D4,
  input  D3,
  input  D2,
  input  D1,
  input  D0,
  input  [1:0] address,
  input  en,
  input  clk,
  output a7,
  output a6,
  output a5,
  output a4,
  output a3,
  output a2,
  output a1,
  output a0
);

  wire and_1_out, and_2_out, and_3_out, and_4_out, and_5_out, and_6_out, and_7_out, and_8_out, and_9_out,
       and_10_out, and_11_out, and_12_out, and_13_out, and_14_out, and_15_out, and_16_out, and_17_out,
       and_18_out, and_19_out, and_20_out, and_21_out, and_22_out, and_23_out, and_24_out, and_25_out,
       and_26_out, and_27_out, and_28_out, and_29_out, and_30_out, and_31_out, and_32_out, and_33_out,
       and_34_out, and_35_out, and_36_out, and_37_out, and_38_out, and_39_out, and_40_out, and_41_out,
       and_42_out, and_43_out, and_44_out, and_45_out, and_46_out, and_47_out, and_48_out, and_49_out,
       and_50_out, and_51_out, and_52_out, and_53_out, and_54_out, and_55_out, and_56_out, and_57_out,
       and_58_out, and_59_out, and_60_out, and_61_out, and_62_out, and_63_out, and_64_out,
       d_flipflop_enable_1_q, d_flipflop_enable_2_q, d_flipflop_enable_3_q, d_flipflop_enable_4_q,
       d_flipflop_enable_5_q, d_flipflop_enable_6_q, d_flipflop_enable_7_q, d_flipflop_enable_8_q,
       d_flipflop_enable_9_q, d_flipflop_enable_10_q, d_flipflop_enable_11_q, d_flipflop_enable_12_q,
       d_flipflop_enable_13_q, d_flipflop_enable_14_q, d_flipflop_enable_15_q, d_flipflop_enable_16_q,
       d_flipflop_enable_17_q, d_flipflop_enable_18_q, d_flipflop_enable_19_q, d_flipflop_enable_20_q,
       d_flipflop_enable_21_q, d_flipflop_enable_22_q, d_flipflop_enable_23_q, d_flipflop_enable_24_q,
       d_flipflop_enable_25_q, d_flipflop_enable_26_q, d_flipflop_enable_27_q, d_flipflop_enable_28_q,
       d_flipflop_enable_29_q, d_flipflop_enable_30_q, d_flipflop_enable_31_q, d_flipflop_enable_32_q;
  wire [3:0] decoder2_4_1_out_3;

  decoder2_4 decoder2_4_1 (.A(address[0]), .B(address[1]), .out_3(decoder2_4_1_out_3));
  and and_1 (and_1_out, decoder2_4_1_out_3[0], en);
  and and_2 (and_2_out, decoder2_4_1_out_3[1], en);
  and and_3 (and_3_out, decoder2_4_1_out_3[2], en);
  and and_4 (and_4_out, decoder2_4_1_out_3[3], en);
  D_FlipFlop_Enable d_flipflop_enable_1 (.D(D7), .en(and_1_out), .clk(clk), .Q(d_flipflop_enable_1_q));
  D_FlipFlop_Enable d_flipflop_enable_2 (.D(D7), .en(and_2_out), .clk(clk), .Q(d_flipflop_enable_2_q));
  D_FlipFlop_Enable d_flipflop_enable_3 (.D(D7), .en(and_3_out), .clk(clk), .Q(d_flipflop_enable_3_q));
  D_FlipFlop_Enable d_flipflop_enable_4 (.D(D7), .en(and_4_out), .clk(clk), .Q(d_flipflop_enable_4_q));
  and and_5 (and_5_out, decoder2_4_1_out_3[0], d_flipflop_enable_1_q);
  and and_6 (and_6_out, decoder2_4_1_out_3[1], d_flipflop_enable_2_q);
  and and_7 (and_7_out, decoder2_4_1_out_3[2], d_flipflop_enable_3_q);
  and and_8 (and_8_out, decoder2_4_1_out_3[3], d_flipflop_enable_4_q);
  or or_1 (a7, and_8_out, and_7_out, and_6_out, and_5_out);
  and and_9 (and_9_out, en, decoder2_4_1_out_3[0]);
  and and_10 (and_10_out, en, decoder2_4_1_out_3[1]);
  and and_11 (and_11_out, en, decoder2_4_1_out_3[2]);
  and and_12 (and_12_out, en, decoder2_4_1_out_3[3]);
  and and_13 (and_13_out, decoder2_4_1_out_3[0], d_flipflop_enable_5_q);
  D_FlipFlop_Enable d_flipflop_enable_5 (.D(D6), .en(and_9_out), .clk(clk), .Q(d_flipflop_enable_5_q));
  and and_14 (and_14_out, decoder2_4_1_out_3[1], d_flipflop_enable_6_q);
  D_FlipFlop_Enable d_flipflop_enable_6 (.D(D6), .en(and_10_out), .clk(clk), .Q(d_flipflop_enable_6_q));
  and and_15 (and_15_out, decoder2_4_1_out_3[2], d_flipflop_enable_7_q);
  D_FlipFlop_Enable d_flipflop_enable_7 (.D(D6), .en(and_11_out), .clk(clk), .Q(d_flipflop_enable_7_q));
  and and_16 (and_16_out, decoder2_4_1_out_3[3], d_flipflop_enable_8_q);
  D_FlipFlop_Enable d_flipflop_enable_8 (.D(D6), .en(and_12_out), .clk(clk), .Q(d_flipflop_enable_8_q));
  or or_2 (a6, and_16_out, and_15_out, and_14_out, and_13_out);
  and and_17 (and_17_out, decoder2_4_1_out_3[0], en);
  and and_18 (and_18_out, decoder2_4_1_out_3[1], en);
  and and_19 (and_19_out, decoder2_4_1_out_3[2], en);
  and and_20 (and_20_out, decoder2_4_1_out_3[3], en);
  and and_21 (and_21_out, decoder2_4_1_out_3[0], d_flipflop_enable_9_q);
  D_FlipFlop_Enable d_flipflop_enable_9 (.D(D5), .en(and_17_out), .clk(clk), .Q(d_flipflop_enable_9_q));
  and and_22 (and_22_out, decoder2_4_1_out_3[1], d_flipflop_enable_10_q);
  D_FlipFlop_Enable d_flipflop_enable_10 (.D(D5), .en(and_18_out), .clk(clk), .Q(d_flipflop_enable_10_q));
  and and_23 (and_23_out, decoder2_4_1_out_3[2], d_flipflop_enable_11_q);
  D_FlipFlop_Enable d_flipflop_enable_11 (.D(D5), .en(and_19_out), .clk(clk), .Q(d_flipflop_enable_11_q));
  and and_24 (and_24_out, decoder2_4_1_out_3[3], d_flipflop_enable_12_q);
  D_FlipFlop_Enable d_flipflop_enable_12 (.D(D5), .en(and_20_out), .clk(clk), .Q(d_flipflop_enable_12_q));
  or or_3 (a5, and_24_out, and_23_out, and_22_out, and_21_out);
  and and_25 (and_25_out, decoder2_4_1_out_3[0], en);
  and and_26 (and_26_out, decoder2_4_1_out_3[1], en);
  and and_27 (and_27_out, decoder2_4_1_out_3[2], en);
  and and_28 (and_28_out, decoder2_4_1_out_3[3], en);
  D_FlipFlop_Enable d_flipflop_enable_13 (.D(D4), .en(and_25_out), .clk(clk), .Q(d_flipflop_enable_13_q));
  D_FlipFlop_Enable d_flipflop_enable_14 (.D(D4), .en(and_26_out), .clk(clk), .Q(d_flipflop_enable_14_q));
  D_FlipFlop_Enable d_flipflop_enable_15 (.D(D4), .en(and_27_out), .clk(clk), .Q(d_flipflop_enable_15_q));
  D_FlipFlop_Enable d_flipflop_enable_16 (.D(D4), .en(and_28_out), .clk(clk), .Q(d_flipflop_enable_16_q));
  and and_29 (and_29_out, decoder2_4_1_out_3[0], d_flipflop_enable_13_q);
  and and_30 (and_30_out, decoder2_4_1_out_3[1], d_flipflop_enable_14_q);
  and and_31 (and_31_out, decoder2_4_1_out_3[2], d_flipflop_enable_15_q);
  and and_32 (and_32_out, decoder2_4_1_out_3[3], d_flipflop_enable_16_q);
  or or_4 (a4, and_32_out, and_31_out, and_30_out, and_29_out);
  and and_33 (and_33_out, decoder2_4_1_out_3[0], en);
  and and_34 (and_34_out, decoder2_4_1_out_3[1], en);
  and and_35 (and_35_out, decoder2_4_1_out_3[2], en);
  and and_36 (and_36_out, decoder2_4_1_out_3[3], en);
  D_FlipFlop_Enable d_flipflop_enable_17 (.D(D3), .en(and_33_out), .clk(clk), .Q(d_flipflop_enable_17_q));
  D_FlipFlop_Enable d_flipflop_enable_18 (.D(D3), .en(and_34_out), .clk(clk), .Q(d_flipflop_enable_18_q));
  D_FlipFlop_Enable d_flipflop_enable_19 (.D(D3), .en(and_35_out), .clk(clk), .Q(d_flipflop_enable_19_q));
  D_FlipFlop_Enable d_flipflop_enable_20 (.D(D3), .en(and_36_out), .clk(clk), .Q(d_flipflop_enable_20_q));
  and and_37 (and_37_out, decoder2_4_1_out_3[0], d_flipflop_enable_17_q);
  and and_38 (and_38_out, decoder2_4_1_out_3[1], d_flipflop_enable_18_q);
  and and_39 (and_39_out, decoder2_4_1_out_3[2], d_flipflop_enable_19_q);
  and and_40 (and_40_out, decoder2_4_1_out_3[3], d_flipflop_enable_20_q);
  or or_5 (a3, and_40_out, and_39_out, and_38_out, and_37_out);
  and and_41 (and_41_out, decoder2_4_1_out_3[0], en);
  and and_42 (and_42_out, decoder2_4_1_out_3[1], en);
  and and_43 (and_43_out, decoder2_4_1_out_3[2], en);
  and and_44 (and_44_out, decoder2_4_1_out_3[3], en);
  D_FlipFlop_Enable d_flipflop_enable_21 (.D(D2), .en(and_41_out), .clk(clk), .Q(d_flipflop_enable_21_q));
  D_FlipFlop_Enable d_flipflop_enable_22 (.D(D2), .en(and_42_out), .clk(clk), .Q(d_flipflop_enable_22_q));
  D_FlipFlop_Enable d_flipflop_enable_23 (.D(D2), .en(and_43_out), .clk(clk), .Q(d_flipflop_enable_23_q));
  D_FlipFlop_Enable d_flipflop_enable_24 (.D(D2), .en(and_44_out), .clk(clk), .Q(d_flipflop_enable_24_q));
  and and_45 (and_45_out, decoder2_4_1_out_3[0], d_flipflop_enable_21_q);
  and and_46 (and_46_out, decoder2_4_1_out_3[1], d_flipflop_enable_22_q);
  and and_47 (and_47_out, decoder2_4_1_out_3[2], d_flipflop_enable_23_q);
  and and_48 (and_48_out, decoder2_4_1_out_3[3], d_flipflop_enable_24_q);
  or or_6 (a2, and_48_out, and_47_out, and_46_out, and_45_out);
  and and_49 (and_49_out, decoder2_4_1_out_3[0], en);
  and and_50 (and_50_out, decoder2_4_1_out_3[1], en);
  and and_51 (and_51_out, decoder2_4_1_out_3[2], en);
  and and_52 (and_52_out, decoder2_4_1_out_3[3], en);
  and and_53 (and_53_out, decoder2_4_1_out_3[0], d_flipflop_enable_25_q);
  D_FlipFlop_Enable d_flipflop_enable_25 (.D(D1), .en(and_49_out), .clk(clk), .Q(d_flipflop_enable_25_q));
  and and_54 (and_54_out, decoder2_4_1_out_3[1], d_flipflop_enable_26_q);
  D_FlipFlop_Enable d_flipflop_enable_26 (.D(D1), .en(and_50_out), .clk(clk), .Q(d_flipflop_enable_26_q));
  and and_55 (and_55_out, decoder2_4_1_out_3[2], d_flipflop_enable_27_q);
  D_FlipFlop_Enable d_flipflop_enable_27 (.D(D1), .en(and_51_out), .clk(clk), .Q(d_flipflop_enable_27_q));
  and and_56 (and_56_out, decoder2_4_1_out_3[3], d_flipflop_enable_28_q);
  D_FlipFlop_Enable d_flipflop_enable_28 (.D(D1), .en(and_52_out), .clk(clk), .Q(d_flipflop_enable_28_q));
  or or_7 (a1, and_56_out, and_55_out, and_54_out, and_53_out);
  and and_57 (and_57_out, decoder2_4_1_out_3[0], en);
  and and_58 (and_58_out, decoder2_4_1_out_3[1], en);
  and and_59 (and_59_out, decoder2_4_1_out_3[2], en);
  and and_60 (and_60_out, decoder2_4_1_out_3[3], en);
  D_FlipFlop_Enable d_flipflop_enable_29 (.D(D0), .en(and_57_out), .clk(clk), .Q(d_flipflop_enable_29_q));
  D_FlipFlop_Enable d_flipflop_enable_30 (.D(D0), .en(and_58_out), .clk(clk), .Q(d_flipflop_enable_30_q));
  D_FlipFlop_Enable d_flipflop_enable_31 (.D(D0), .en(and_59_out), .clk(clk), .Q(d_flipflop_enable_31_q));
  D_FlipFlop_Enable d_flipflop_enable_32 (.D(D0), .en(and_60_out), .clk(clk), .Q(d_flipflop_enable_32_q));
  and and_61 (and_61_out, decoder2_4_1_out_3[0], d_flipflop_enable_29_q);
  and and_62 (and_62_out, decoder2_4_1_out_3[1], d_flipflop_enable_30_q);
  and and_63 (and_63_out, decoder2_4_1_out_3[2], d_flipflop_enable_31_q);
  and and_64 (and_64_out, decoder2_4_1_out_3[3], d_flipflop_enable_32_q);
  or or_8 (a0, and_64_out, and_63_out, and_62_out, and_61_out);
endmodule

module ROM_8_8 (
  input  [1:0] in_1,
  input  clk,
  output [7:0] out_3
);

  wire and_1_out, and_2_out, and_3_out, and_4_out, and_5_out, and_6_out, and_7_out, and_8_out, and_9_out,
       and_10_out, and_11_out, and_12_out, and_13_out, and_14_out, and_15_out, and_16_out, and_17_out,
       and_18_out, and_19_out, and_20_out, and_21_out, and_22_out, and_23_out, and_24_out, and_25_out,
       and_26_out, and_27_out, and_28_out, and_29_out, and_30_out, and_31_out, and_32_out, and_33_out,
       and_34_out, and_35_out, and_36_out, and_37_out, and_38_out, and_39_out, and_40_out, and_41_out,
       and_42_out, and_43_out, and_44_out, and_45_out, and_46_out, and_47_out, and_48_out, and_49_out,
       and_50_out, and_51_out, and_52_out, and_53_out, and_54_out, and_55_out, and_56_out, and_57_out,
       and_58_out, and_59_out, and_60_out, and_61_out, and_62_out, and_63_out, and_64_out, or_1_out,
       or_2_out, or_3_out, or_4_out, or_5_out, or_6_out, or_7_out, or_8_out;
  wire [3:0] decoder2_4_1_out_3;

  decoder2_4 decoder2_4_1 (.A(in_1[0]), .B(in_1[1]), .out_3(decoder2_4_1_out_3));
  and and_1 (and_1_out, decoder2_4_1_out_3[0], 1'b1);
  and and_2 (and_2_out, decoder2_4_1_out_3[1], 1'b1);
  and and_3 (and_3_out, decoder2_4_1_out_3[2], 1'b1);
  and and_4 (and_4_out, decoder2_4_1_out_3[3], 1'b1);
  and and_5 (and_5_out, 1'b0, 1'b0);
  and and_6 (and_6_out, 1'b0, 1'b0);
  and and_7 (and_7_out, 1'b0, 1'b1);
  and and_8 (and_8_out, 1'b0, 1'b1);
  or or_1 (or_1_out, and_8_out, and_7_out, and_6_out, and_5_out, and_4_out, and_3_out, and_2_out, and_1_out);
  and and_9 (and_9_out, decoder2_4_1_out_3[0], 1'b0);
  and and_10 (and_10_out, decoder2_4_1_out_3[1], 1'b0);
  and and_11 (and_11_out, decoder2_4_1_out_3[2], 1'b0);
  and and_12 (and_12_out, decoder2_4_1_out_3[3], 1'b0);
  and and_13 (and_13_out, 1'b0, 1'b0);
  and and_14 (and_14_out, 1'b0, 1'b0);
  and and_15 (and_15_out, 1'b0, 1'b1);
  and and_16 (and_16_out, 1'b0, 1'b1);
  or or_2 (or_2_out, and_16_out, and_15_out, and_14_out, and_13_out, and_12_out, and_11_out, and_10_out, and_9_out);
  and and_17 (and_17_out, decoder2_4_1_out_3[0], 1'b0);
  and and_18 (and_18_out, decoder2_4_1_out_3[1], 1'b0);
  and and_19 (and_19_out, decoder2_4_1_out_3[2], 1'b1);
  and and_20 (and_20_out, decoder2_4_1_out_3[3], 1'b1);
  and and_21 (and_21_out, 1'b0, 1'b0);
  and and_22 (and_22_out, 1'b0, 1'b1);
  and and_23 (and_23_out, 1'b0, 1'b0);
  and and_24 (and_24_out, 1'b0, 1'b0);
  or or_3 (or_3_out, and_24_out, and_23_out, and_22_out, and_21_out, and_20_out, and_19_out, and_18_out, and_17_out);
  and and_25 (and_25_out, decoder2_4_1_out_3[0], 1'b0);
  and and_26 (and_26_out, decoder2_4_1_out_3[1], 1'b1);
  and and_27 (and_27_out, decoder2_4_1_out_3[2], 1'b0);
  and and_28 (and_28_out, decoder2_4_1_out_3[3], 1'b1);
  and and_29 (and_29_out, 1'b0, 1'b1);
  and and_30 (and_30_out, 1'b0, 1'b0);
  and and_31 (and_31_out, 1'b0, 1'b1);
  and and_32 (and_32_out, 1'b0, 1'b1);
  or or_4 (or_4_out, and_32_out, and_31_out, and_30_out, and_29_out, and_28_out, and_27_out, and_26_out, and_25_out);
  and and_33 (and_33_out, decoder2_4_1_out_3[0], 1'b1);
  and and_34 (and_34_out, decoder2_4_1_out_3[1], 1'b0);
  and and_35 (and_35_out, decoder2_4_1_out_3[2], 1'b0);
  and and_36 (and_36_out, decoder2_4_1_out_3[3], 1'b0);
  and and_37 (and_37_out, 1'b0, 1'b0);
  and and_38 (and_38_out, 1'b0, 1'b1);
  and and_39 (and_39_out, 1'b0, 1'b0);
  and and_40 (and_40_out, 1'b0, 1'b1);
  or or_5 (or_5_out, and_40_out, and_39_out, and_38_out, and_37_out, and_36_out, and_35_out, and_34_out, and_33_out);
  and and_41 (and_41_out, decoder2_4_1_out_3[0], 1'b0);
  and and_42 (and_42_out, decoder2_4_1_out_3[1], 1'b0);
  and and_43 (and_43_out, decoder2_4_1_out_3[2], 1'b0);
  and and_44 (and_44_out, decoder2_4_1_out_3[3], 1'b0);
  and and_45 (and_45_out, 1'b0, 1'b1);
  and and_46 (and_46_out, 1'b0, 1'b0);
  and and_47 (and_47_out, 1'b0, 1'b0);
  and and_48 (and_48_out, 1'b0, 1'b1);
  or or_6 (or_6_out, and_48_out, and_47_out, and_46_out, and_45_out, and_44_out, and_43_out, and_42_out, and_41_out);
  and and_49 (and_49_out, decoder2_4_1_out_3[0], 1'b1);
  and and_50 (and_50_out, decoder2_4_1_out_3[1], 1'b0);
  and and_51 (and_51_out, decoder2_4_1_out_3[2], 1'b0);
  and and_52 (and_52_out, decoder2_4_1_out_3[3], 1'b0);
  and and_53 (and_53_out, 1'b0, 1'b1);
  and and_54 (and_54_out, 1'b0, 1'b0);
  and and_55 (and_55_out, 1'b0, 1'b0);
  and and_56 (and_56_out, 1'b0, 1'b1);
  or or_7 (or_7_out, and_56_out, and_55_out, and_54_out, and_53_out, and_52_out, and_51_out, and_50_out, and_49_out);
  and and_57 (and_57_out, decoder2_4_1_out_3[0], 1'b0);
  and and_58 (and_58_out, decoder2_4_1_out_3[1], 1'b0);
  and and_59 (and_59_out, decoder2_4_1_out_3[2], 1'b0);
  and and_60 (and_60_out, decoder2_4_1_out_3[3], 1'b1);
  and and_61 (and_61_out, 1'b0, 1'b1);
  and and_62 (and_62_out, 1'b0, 1'b1);
  and and_63 (and_63_out, 1'b0, 1'b1);
  and and_64 (and_64_out, 1'b0, 1'b1);
  or or_8 (or_8_out, and_64_out, and_63_out, and_62_out, and_61_out, and_60_out, and_59_out, and_58_out, and_57_out);
  register_8 register_8_1 (
    .D7(or_1_out), .D6(or_2_out), .D5(or_3_out), .D4(or_4_out), .D3(or_5_out), .D2(or_6_out), .D1(or_7_out),
    .D0(or_8_out), .reset(1'b1), .en(1'b1), .clk(clk), .Q7(out_3[7]), .Q6(out_3[6]), .Q5(out_3[5]),
    .Q4(out_3[4]), .Q3(out_3[3]), .Q2(out_3[2]), .Q1(out_3[1]), .Q0(out_3[0]));
endmodule

module decoder2_4 (
  input  A,
  input  B,
  output [3:0] out_3
);

  and and_1 (out_3[0], ~A, ~B);  // AND_Gate
  and and_2 (out_3[1], A, ~B);  // AND_Gate
  and and_3 (out_3[2], ~A, B);  // AND_Gate
  and and_4 (out_3[3], A, B);
endmodule

module decoder3_8 (
  input  A,
  input  B,
  input  C,
  output Y0,
  output Y1,
  output Y2,
  output Y3,
  output Y4,
  output Y5,
  output Y6,
  output Y7
);

  wire [3:0] decoder2_4_1_out_3, decoder2_4_2_out_3;

  decoder2_4 decoder2_4_1 (.A(A), .B(B), .out_3(decoder2_4_1_out_3));
  decoder2_4 decoder2_4_2 (.A(A), .B(B), .out_3(decoder2_4_2_out_3));
  assign {Y3, Y2, Y1, Y0} = decoder2_4_1_out_3 & ~{4{C}};  // AND_Gate and_1, 4 bits wide
  assign {Y7, Y6, Y5, Y4} = decoder2_4_2_out_3 & {4{C}};  // AND_Gate and_2, 4 bits wide
endmodule

module SRlatch (
  input  S,
  input  R,
  output Q,
  output Q1
);

  nor nor_1 (Q, R, Q1);
  nor nor_2 (Q1, Q, S);
endmodule

module DLatch (
  input  D,
  input  en,
  output Q,
  output Q1
);

  wire and_1_out, and_2_out;

  and and_1 (and_1_out, D, en);
  and and_2 (and_2_out, en, ~D);  // AND_Gate
  SRlatch srlatch_1 (.S(and_1_out), .R(and_2_out), .Q(Q), .Q1(Q1));
endmodule

module Toggling_D_Latch_Reset (
  input  D,
  input  en,
  input  reset,
  output Q,
  output Q1
);

  wire and_1_out, and_2_out, or_1_out;

  and and_1 (and_1_out, D, ~reset, en);  // AND_Gate
  and and_2 (and_2_out, en, ~D);  // AND_Gate
  or or_1 (or_1_out, and_2_out, reset);
  SRlatch srlatch_1 (.S(and_1_out), .R(or_1_out), .Q(Q), .Q1(Q1));
endmodule

module D_Flip_Flop (
  input  D,
  input  clk,
  output Q
);

  wire dlatch_1_q, not_1_out;

  not not_1 (not_1_out, clk);
  DLatch dlatch_1 (.D(D), .en(not_1_out), .Q(dlatch_1_q));  // open: Q1
  DLatch dlatch_2 (.D(dlatch_1_q), .en(clk), .Q(Q));  // open: Q1
endmodule

module D_FlipFlop_SyncReset (
  input  D,
  input  RESET,
  input  CLK,
  output Q
);

  wire and_1_out;

  and and_1 (and_1_out, D, RESET);
  D_Flip_Flop d_flip_flop_1 (.D(and_1_out), .clk(CLK), .Q(Q));
endmodule

module D_FlipFlop_Enable (
  input  D,
  input  en,
  input  clk,
  output Q
);

  wire multiplexer_1_out;

  Multiplexer multiplexer_1 (.in0(Q), .in1(D), .out(multiplexer_1_out), .sel(en));
  D_Flip_Flop d_flip_flop_1 (.D(multiplexer_1_out), .clk(clk), .Q(Q));
endmodule

module T_FlipFlop_From_DFF (
  input  in_1,
  input  in_2,
  output out_3
);

  wire not_1_out;

  D_FlipFlop_SyncReset d_flipflop_syncreset_1 (.D(not_1_out), .RESET(in_1), .CLK(in_2), .Q(out_3));
  not not_1 (not_1_out, out_3);
endmodule

module register_8 (
  input  D7,
  input  D6,
  input  D5,
  input  D4,
  input  D3,
  input  D2,
  input  D1,
  input  D0,
  input  reset,
  input  en,
  input  clk,
  output Q7,
  output Q6,
  output Q5,
  output Q4,
  output Q3,
  output Q2,
  output Q1,
  output Q0
);

  wire and_1_out, and_2_out, and_3_out, and_4_out, and_5_out, and_6_out, and_7_out, and_8_out;

  and and_1 (and_1_out, reset, D7);
  D_FlipFlop_Enable d_flipflop_enable_1 (.D(and_1_out), .en(en), .clk(clk), .Q(Q7));
  and and_2 (and_2_out, reset, D6);
  D_FlipFlop_Enable d_flipflop_enable_2 (.D(and_2_out), .en(en), .clk(clk), .Q(Q6));
  and and_3 (and_3_out, reset, D5);
  D_FlipFlop_Enable d_flipflop_enable_3 (.D(and_3_out), .en(en), .clk(clk), .Q(Q5));
  and and_4 (and_4_out, reset, D4);
  D_FlipFlop_Enable d_flipflop_enable_4 (.D(and_4_out), .en(en), .clk(clk), .Q(Q4));
  and and_5 (and_5_out, reset, D3);
  D_FlipFlop_Enable d_flipflop_enable_5 (.D(and_5_out), .en(en), .clk(clk), .Q(Q3));
  and and_6 (and_6_out, reset, D2);
  D_FlipFlop_Enable d_flipflop_enable_6 (.D(and_6_out), .en(en), .clk(clk), .Q(Q2));
  and and_7 (and_7_out, reset, D1);
  D_FlipFlop_Enable d_flipflop_enable_7 (.D(and_7_out), .en(en), .clk(clk), .Q(Q1));
  and and_8 (and_8_out, reset, D0);
  D_FlipFlop_Enable d_flipflop_enable_8 (.D(and_8_out), .en(en), .clk(clk), .Q(Q0));
endmodule

module counter_4bit (
  input  reset,
  input  en,
  input  fuweien,
  input  clk,
  input  fuweiclk,
  output d4,
  output d3,
  output d2,
  output d1
);

  wire and_1_out, and_2_out, and_3_out, and_4_out, or_1_out, or_2_out, rca_4bit_1_first, rca_4bit_1_fourth,
       rca_4bit_1_second, rca_4bit_1_third;

  RCA_4bit rca_4bit_1 (
    .a4(d4), .a3(d3), .a2(d2), .a1(d1), .b1(1'b1), .first(rca_4bit_1_first), .second(rca_4bit_1_second),
    .third(rca_4bit_1_third), .fourth(rca_4bit_1_fourth));  // open: b4, b3, b2
  and and_1 (and_1_out, rca_4bit_1_first, reset);
  and and_2 (and_2_out, rca_4bit_1_second, reset);
  and and_3 (and_3_out, rca_4bit_1_third, reset);
  and and_4 (and_4_out, rca_4bit_1_fourth, reset);
  or or_1 (or_1_out, en, fuweien);
  or or_2 (or_2_out, clk, fuweiclk);
  Register_4bit register_4bit_1 (
    .c1(and_1_out), .c2(and_2_out), .c3(and_3_out), .c4(and_4_out), .en(or_1_out), .clk(or_2_out), .d4(d4),
    .d3(d3), .d2(d2), .d1(d1));
  Hex_Digit_Display hex_digit_display_1 (.value({d4, d3, d2, d1}));  // open: dp
endmodule

module RCA_4bit (
  input  a4,
  input  a3,
  input  a2,
  input  a1,
  input  b4,
  input  b3,
  input  b2,
  input  b1,
  output first,
  output second,
  output third,
  output fourth
);

  wire fulladder_1_cout, fulladder_2_cout, fulladder_3_cout, halfadder_1_c, hex_7segment_decoder_1_a1,
       hex_7segment_decoder_1_b1, hex_7segment_decoder_1_c1, hex_7segment_decoder_1_d1,
       hex_7segment_decoder_1_e1, hex_7segment_decoder_1_f1, hex_7segment_decoder_1_g1,
       hex_7segment_decoder_2_a1, hex_7segment_decoder_2_b1, hex_7segment_decoder_2_c1,
       hex_7segment_decoder_2_d1, hex_7segment_decoder_2_e1, hex_7segment_decoder_2_f1,
       hex_7segment_decoder_2_g1, hex_7segment_decoder_3_a1, hex_7segment_decoder_3_b1,
       hex_7segment_decoder_3_c1, hex_7segment_decoder_3_d1, hex_7segment_decoder_3_e1,
       hex_7segment_decoder_3_f1, hex_7segment_decoder_3_g1;

  fulladder fulladder_1 (.A(a4), .B(b4), .Cin(fulladder_2_cout), .S(fourth), .Cout(fulladder_1_cout));
  fulladder fulladder_2 (.A(a3), .B(b3), .Cin(fulladder_3_cout), .S(third), .Cout(fulladder_2_cout));
  fulladder fulladder_3 (.A(a2), .B(b2), .Cin(halfadder_1_c), .S(second), .Cout(fulladder_3_cout));
  halfadder halfadder_1 (.A(a1), .B(b1), .S(first), .C(halfadder_1_c));
  LED led_1 (.in(fulladder_1_cout));
  Hex_7Segment_Decoder hex_7segment_decoder_1 (
    .in_1({fourth, third, second, first}), .a1(hex_7segment_decoder_1_a1), .b1(hex_7segment_decoder_1_b1),
    .c1(hex_7segment_decoder_1_c1), .d1(hex_7segment_decoder_1_d1), .e1(hex_7segment_decoder_1_e1),
    .f1(hex_7segment_decoder_1_f1), .g1(hex_7segment_decoder_1_g1));
  _7_Segment_Display u_7_segment_display_1 (
    .g(hex_7segment_decoder_1_g1), .f(hex_7segment_decoder_1_f1), .a(hex_7segment_decoder_1_a1),
    .b(hex_7segment_decoder_1_b1), .e(hex_7segment_decoder_1_e1), .d(hex_7segment_decoder_1_d1),
    .c(hex_7segment_decoder_1_c1));  // open: dp
  Hex_7Segment_Decoder hex_7segment_decoder_2 (
    .in_1({a4, a3, a2, a1}), .a1(hex_7segment_decoder_2_a1), .b1(hex_7segment_decoder_2_b1),
    .c1(hex_7segment_decoder_2_c1), .d1(hex_7segment_decoder_2_d1), .e1(hex_7segment_decoder_2_e1),
    .f1(hex_7segment_decoder_2_f1), .g1(hex_7segment_decoder_2_g1));
  Hex_7Segment_Decoder hex_7segment_decoder_3 (
    .in_1({b4, b3, b2, b1}), .a1(hex_7segment_decoder_3_a1), .b1(hex_7segment_decoder_3_b1),
    .c1(hex_7segment_decoder_3_c1), .d1(hex_7segment_decoder_3_d1), .e1(hex_7segment_decoder_3_e1),
    .f1(hex_7segment_decoder_3_f1), .g1(hex_7segment_decoder_3_g1));
  _7_Segment_Display u_7_segment_display_2 (
    .g(hex_7segment_decoder_2_g1), .f(hex_7segment_decoder_2_f1), .a(hex_7segment_decoder_2_a1),
    .b(hex_7segment_decoder_2_b1), .e(hex_7segment_decoder_2_e1), .d(hex_7segment_decoder_2_d1),
    .c(hex_7segment_decoder_2_c1));  // open: dp
  _7_Segment_Display u_7_segment_display_3 (
    .g(hex_7segment_decoder_3_g1), .f(hex_7segment_decoder_3_f1), .a(hex_7segment_decoder_3_a1),
    .b(hex_7segment_decoder_3_b1), .e(hex_7segment_decoder_3_e1), .d(hex_7segment_decoder_3_d1),
    .c(hex_7segment_decoder_3_c1));  // open: dp
endmodule

module Register_4bit (
  input  c1,
  input  c2,
  input  c3,
  input  c4,
  input  en,
  input  clk,
  output d4,
  output d3,
  output d2,
  output d1
);

  Enabled_DFF enabled_dff_1 (.en(en), .D(c4), .clk(clk), .Q(d4));
  Enabled_DFF enabled_dff_2 (.en(en), .D(c3), .clk(clk), .Q(d3));
  Enabled_DFF enabled_dff_3 (.en(en), .D(c2), .clk(clk), .Q(d2));
  Hex_Digit_Display hex_digit_display_1 (.value({d4, d3, d2, d1}));  // open: dp
  Enabled_DFF enabled_dff_4 (.en(en), .D(c1), .clk(clk), .Q(d1));
endmodule

module Enabled_DFF (
  input  en,
  input  D,
  input  clk,
  output Q
);

  wire dlatch_1_q, multiplexer_1_out, not_1_out;

  Multiplexer multiplexer_1 (.in0(Q), .in1(D), .out(multiplexer_1_out), .sel(en));
  not not_1 (not_1_out, clk);
  DLatch dlatch_1 (.D(multiplexer_1_out), .en(not_1_out), .Q(dlatch_1_q));  // open: Q1
  DLatch dlatch_2 (.D(dlatch_1_q), .en(clk), .Q(Q));  // open: Q1
endmodule

module halfadder (
  input  A,
  input  B,
  output S,
  output C
);

  and and_1 (C, A, B);
  xor xor_1 (S, A, B);
endmodule

module fulladder (
  input  A,
  input  B,
  input  Cin,
  output S,
  output Cout
);

  wire halfadder_1_c, halfadder_1_s, halfadder_2_c;

  halfadder halfadder_1 (.A(A), .B(B), .S(halfadder_1_s), .C(halfadder_1_c));
  halfadder halfadder_2 (.A(halfadder_1_s), .B(Cin), .S(S), .C(halfadder_2_c));
  or or_1 (Cout, halfadder_2_c, halfadder_1_c);
endmodule

module decoder4_16 (
  input  Y1,
  input  Y2,
  input  Y3,
  input  Y4,
  output [15:0] out_5
);

  wire [7:0] decoder3_8_1_y0, decoder3_8_2_y0;

  decoder3_8 decoder3_8_1 (
    .A(Y1), .B(Y2), .C(Y3), .Y0(decoder3_8_1_y0[0]), .Y1(decoder3_8_1_y0[1]), .Y2(decoder3_8_1_y0[2]),
    .Y3(decoder3_8_1_y0[3]), .Y4(decoder3_8_1_y0[4]), .Y5(decoder3_8_1_y0[5]), .Y6(decoder3_8_1_y0[6]),
    .Y7(decoder3_8_1_y0[7]));
  decoder3_8 decoder3_8_2 (
    .A(Y1), .B(Y2), .C(Y3), .Y0(decoder3_8_2_y0[0]), .Y1(decoder3_8_2_y0[1]), .Y2(decoder3_8_2_y0[2]),
    .Y3(decoder3_8_2_y0[3]), .Y4(decoder3_8_2_y0[4]), .Y5(decoder3_8_2_y0[5]), .Y6(decoder3_8_2_y0[6]),
    .Y7(decoder3_8_2_y0[7]));
  assign out_5[7:0] = decoder3_8_1_y0 & ~{8{Y4}};  // AND_Gate and_1, 8 bits wide
  assign out_5[15:8] = decoder3_8_2_y0 & {8{Y4}};  // AND_Gate and_2, 8 bits wide
endmodule

module Hex_7Segment_Decoder (
  input  [3:0] in_1,
  output a1,
  output b1,
  output c1,
  output d1,
  output e1,
  output f1,
  output g1
);

  wire [15:0] decoder4_16_1_out_5;

  decoder4_16 decoder4_16_1 (.Y1(in_1[0]), .Y2(in_1[1]), .Y3(in_1[2]), .Y4(in_1[3]), .out_5(decoder4_16_1_out_5));
  or d (d1, decoder4_16_1_out_5[0], decoder4_16_1_out_5[2], decoder4_16_1_out_5[3], decoder4_16_1_out_5[5], decoder4_16_1_out_5[6], decoder4_16_1_out_5[14], decoder4_16_1_out_5[8], decoder4_16_1_out_5[9], decoder4_16_1_out_5[11], decoder4_16_1_out_5[12], decoder4_16_1_out_5[13]);
  or e (e1, decoder4_16_1_out_5[0], decoder4_16_1_out_5[2], decoder4_16_1_out_5[6], decoder4_16_1_out_5[8], decoder4_16_1_out_5[10], decoder4_16_1_out_5[11], decoder4_16_1_out_5[12], decoder4_16_1_out_5[13], decoder4_16_1_out_5[15], decoder4_16_1_out_5[14]);
  or c (c1, decoder4_16_1_out_5[0], decoder4_16_1_out_5[1], decoder4_16_1_out_5[3], decoder4_16_1_out_5[4], decoder4_16_1_out_5[11], decoder4_16_1_out_5[5], decoder4_16_1_out_5[7], decoder4_16_1_out_5[8], decoder4_16_1_out_5[9], decoder4_16_1_out_5[10], decoder4_16_1_out_5[13], decoder4_16_1_out_5[6]);
  or g (g1, decoder4_16_1_out_5[14], decoder4_16_1_out_5[8], decoder4_16_1_out_5[2], decoder4_16_1_out_5[3], decoder4_16_1_out_5[4], decoder4_16_1_out_5[6], decoder4_16_1_out_5[15], decoder4_16_1_out_5[9], decoder4_16_1_out_5[10], decoder4_16_1_out_5[11], decoder4_16_1_out_5[13], decoder4_16_1_out_5[5]);
  or f (f1, decoder4_16_1_out_5[0], decoder4_16_1_out_5[4], decoder4_16_1_out_5[5], decoder4_16_1_out_5[6], decoder4_16_1_out_5[8], decoder4_16_1_out_5[14], decoder4_16_1_out_5[9], decoder4_16_1_out_5[10], decoder4_16_1_out_5[11], decoder4_16_1_out_5[12], decoder4_16_1_out_5[15]);
  or a (a1, decoder4_16_1_out_5[15], decoder4_16_1_out_5[0], decoder4_16_1_out_5[2], decoder4_16_1_out_5[3], decoder4_16_1_out_5[5], decoder4_16_1_out_5[6], decoder4_16_1_out_5[7], decoder4_16_1_out_5[8], decoder4_16_1_out_5[9], decoder4_16_1_out_5[10], decoder4_16_1_out_5[12], decoder4_16_1_out_5[14]);
  or b (b1, decoder4_16_1_out_5[13], decoder4_16_1_out_5[10], decoder4_16_1_out_5[9], decoder4_16_1_out_5[8], decoder4_16_1_out_5[7], decoder4_16_1_out_5[4], decoder4_16_1_out_5[3], decoder4_16_1_out_5[2], decoder4_16_1_out_5[1], decoder4_16_1_out_5[0]);
endmodule
