// Logisim project scpu_sum_1to10.circ as structural Verilog: 1 circuit, main circuit main
module main (
);

  wire add, and_1_out, and_2_out, and_3_out, and_4_out, benr0, clock_1_out, clock_2_out, comparator_1_eq,
       decoder_1_out0, decoder_1_out1, decoder_1_out2, decoder_1_out3, li, load, reset, WE;
  wire [2:0] addr, PC;
  wire [7:0] add_result, bit_extender_1_out, CMD, register_2_q, register_3_q, register_4_q, rs0_data,
       rs1_data, rs2_data, write_data;

  Counter #(.max('h7), .width(3)) counter_1 (
    .clr(reset), .load(load), .clk(clock_1_out), .D(addr), .Q(PC));  // open: up, count, carry
  Clock clock_1 (.out(clock_1_out));
  // Probe on addr
  Button button_1 (.out(reset));
  Adder adder_1 (.a(rs1_data), .b(rs2_data), .out(add_result));  // open: cin, cout
  assign bit_extender_1_out = {{4{1'b0}}, {addr[1:0], CMD[1:0]}};  // Bit_Extender bit_extender_1
  Multiplexer #(.select(2), .width(8)) multiplexer_1 (
    .in0(add_result), .in2(bit_extender_1_out), .out(write_data), .sel(CMD[7:6]));  // open: in1, in3
  ROM #(.addrWidth(3)) rom_1 (.addr(PC), .data({CMD[7:5], addr, CMD[1:0]}));
  Clock clock_2 (.out(clock_2_out));
  Decoder #(.select(2)) decoder_1 (
    .out0(decoder_1_out0), .out1(decoder_1_out1), .out2(decoder_1_out2), .out3(decoder_1_out3),
    .sel({CMD[5], addr[2]}));  // open: en
  // Probe on {CMD[7:5], addr, CMD[1:0]}
  Decoder #(.select(2)) decoder_2 (.out0(add), .out2(li), .out3(benr0), .sel(CMD[7:6]));  // open: out1, en
  or or_1 (WE, add, li);
  and and_1 (and_1_out, decoder_1_out0, WE);
  and and_2 (and_2_out, decoder_1_out1, WE);
  and and_3 (and_3_out, decoder_1_out2, WE);
  and and_4 (and_4_out, decoder_1_out3, WE);
  Register register_1 (.D(write_data), .en(and_1_out), .clk(clock_2_out), .Q(rs0_data), .clr(reset));
  Register register_2 (.D(write_data), .en(and_2_out), .clk(clock_2_out), .Q(register_2_q), .clr(reset));
  Register register_3 (.D(write_data), .en(and_3_out), .clk(clock_2_out), .Q(register_3_q), .clr(reset));
  Register register_4 (.D(write_data), .en(and_4_out), .clk(clock_2_out), .Q(register_4_q), .clr(reset));
  Comparator comparator_1 (.a(rs0_data), .b(rs2_data), .eq(comparator_1_eq));  // open: gt, lt
  and and_5 (load, benr0, ~comparator_1_eq);  // AND_Gate
  Multiplexer #(.select(2), .width(8)) multiplexer_2 (
    .in0(rs0_data), .in1(register_2_q), .in2(register_3_q), .in3(register_4_q), .out(rs1_data),
    .sel(addr[1:0]));
  Multiplexer #(.select(2), .width(8)) multiplexer_3 (
    .in0(rs0_data), .in1(register_2_q), .in2(register_3_q), .in3(register_4_q), .out(rs2_data), .sel(CMD[1:0]));
  // Probe on register_3_q

  // Other names for the same wires on the sheet: imm[3:0] = {addr[1:0], CMD[1:0]}; rs2[1:0] = CMD[1:0];
  //   CMD[4:2] = addr; rs1[1:0] = addr[1:0]; op_code[1:0] = CMD[7:6]; rd[1:0] = {CMD[5], addr[2]}

  // Notes on the sheet:
  //   COUNTER
  //   CMD
  //   contents of rom_1 (hex, n*v repeats v):
  //   8a 90 a0 b1 17 29 d1 df
  //   ROM
  //   op_code
  //   1+3+5+7+9
  //   1+2+3+4+5+6+7+8+9+10
  //   8b_91_a0_b2_29_17_d1_df
  //   8a_90_a0_b1_17_29_d1_df
endmodule
