// Logisim project scpu_sum_1to10_enhanced.circ as structural Verilog: 1 circuit, main circuit main
module main (
);

  wire add, and_1_out, and_2_out, and_3_out, and_4_out, and_5_out, and_7_out, and_9_out, benr0, clock_1_out,
       clock_2_out, clock_3_out, clock_4_out, comparator_1_eq, comparator_2_eq, comparator_3_eq,
       comparator_4_eq, comparator_5_eq, decoder_1_out0, decoder_1_out1, decoder_1_out2, decoder_1_out3, io,
       li, load, reset, WE;
  wire [3:0] addr, PC;
  wire [7:0] add_result, and_8_out, and_10_out, and_11_out, bit_extender_1_out, bit_extender_2_out,
       bit_extender_3_out, bit_extender_4_out, bit_extender_5_out, button_2_out, CMD, imm_result, ioinput,
       ool_out, r0_result, r1_result, r2_result, r3_result, rd_result, register_5_q, register_6_q, rs1_data,
       rs2_data, shifter_1_out, shifter_2_out, shifter_3_out, undriven, write_data;

  Counter #(.max('hf), .width(4)) counter_1 (
    .clr(reset), .load(load), .clk(clock_1_out), .D(addr), .Q(PC));  // open: up, count, carry
  Clock clock_1 (.out(clock_1_out));
  // Probe on addr
  Button button_1 (.out(reset));
  Adder adder_1 (.a(rs1_data), .b(rs2_data), .out(add_result));  // open: cin, cout
  Multiplexer #(.select(2), .width(8)) multiplexer_1 (
    .in0(add_result), .in1(ioinput), .in2(imm_result), .out(write_data), .sel(CMD[7:6]));  // open: in3
  ROM #(.addrWidth(4)) rom_1 (.addr(PC), .data(CMD));
  Clock clock_2 (.out(clock_2_out));
  Decoder #(.select(2)) decoder_1 (
    .out0(decoder_1_out0), .out1(decoder_1_out1), .out2(decoder_1_out2), .out3(decoder_1_out3), .sel(CMD[5:4]));  // open: en
  // Probe on CMD
  Decoder #(.select(2)) decoder_2 (.out0(add), .out1(io), .out2(li), .out3(benr0), .sel(CMD[7:6]));  // open: en
  and and_1 (and_1_out, io, ~CMD[3]);  // AND_Gate
  or or_1 (WE, add, and_1_out, li);
  and and_2 (and_2_out, decoder_1_out0, WE);
  and and_3 (and_3_out, decoder_1_out1, WE);
  and and_4 (and_4_out, decoder_1_out2, WE);
  and and_5 (and_5_out, decoder_1_out3, WE);
  Register register_1 (.D(write_data), .en(and_2_out), .clk(clock_2_out), .Q(r0_result), .clr(reset));
  Register register_2 (.D(write_data), .en(and_3_out), .clk(clock_2_out), .Q(r1_result), .clr(reset));
  Register register_3 (.D(write_data), .en(and_4_out), .clk(clock_2_out), .Q(r2_result), .clr(reset));
  Register register_4 (.D(write_data), .en(and_5_out), .clk(clock_2_out), .Q(r3_result), .clr(reset));
  assign bit_extender_1_out = {{6{1'b0}}, CMD[1:0]};  // Bit_Extender bit_extender_1
  Multiplexer #(.select(2), .width(8)) multiplexer_2 (
    .in0(r0_result), .in1(r1_result), .in2(r2_result), .in3(r3_result), .out(rd_result), .sel(CMD[5:4]));
  Comparator comparator_1 (.a(r0_result), .b(rs2_data), .eq(comparator_1_eq));  // open: gt, lt
  // LedBar #(.inputtype("row")) ledbar_1: pin names not known; wires that end beside it: r0_result
  Shifter shifter_1 (.in(bit_extender_1_out), .\dist (3'b010), .out(shifter_1_out));
  Shifter shifter_2 (.in(bit_extender_1_out), .\dist (3'b100), .out(shifter_2_out));
  Shifter shifter_3 (.in(bit_extender_1_out), .\dist (3'b110), .out(shifter_3_out));
  and and_6 (load, benr0, ~comparator_1_eq);  // AND_Gate
  Multiplexer #(.select(2), .width(8)) multiplexer_3 (
    .in0(r0_result), .in1(r1_result), .in2(r2_result), .in3(r3_result), .out(rs1_data), .sel(CMD[3:2]));
  Multiplexer #(.select(2), .width(8)) multiplexer_4 (
    .in0(r0_result), .in1(r1_result), .in2(r2_result), .in3(r3_result), .out(rs2_data), .sel(CMD[1:0]));
  // Probe on r2_result
  Multiplexer #(.select(2), .width(8)) multiplexer_5 (
    .in0(bit_extender_1_out), .in1(shifter_1_out), .in2(shifter_2_out), .in3(shifter_3_out),
    .out(imm_result), .sel(CMD[3:2]));
  Adder #(.width(4)) adder_2 (.a(PC), .b(CMD[5:2]), .out(addr));  // open: cin, cout
  // DipSwitch dipswitch_1: pin names not known
  Button button_2 (.out(button_2_out[0]));
  Button button_3 (.out(button_2_out[1]));
  Button button_4 (.out(button_2_out[2]));
  Button button_5 (.out(button_2_out[3]));
  Button button_6 (.out(button_2_out[4]));
  Button button_7 (.out(button_2_out[5]));
  Button button_8 (.out(button_2_out[6]));
  Button button_9 (.out(button_2_out[7]));
  Comparator #(.width(3)) comparator_2 (.a(CMD[2:0]), .b(3'b000), .eq(comparator_2_eq));  // open: gt, lt
  assign bit_extender_2_out = {{7{1'b1}}, comparator_2_eq};  // Bit_Extender bit_extender_2
  and and_7 (and_7_out, comparator_3_eq, io, CMD[3]);
  assign and_8_out = {8{io}} & bit_extender_2_out & rd_result;  // AND_Gate and_8, 8 bits wide
  and and_9 (and_9_out, io, comparator_2_eq);
  Comparator #(.width(3)) comparator_3 (.a(CMD[2:0]), .b(3'b001), .eq(comparator_3_eq));  // open: gt, lt
  assign bit_extender_3_out = {{7{1'b1}}, comparator_3_eq};  // Bit_Extender bit_extender_3
  Comparator #(.width(3)) comparator_4 (.a(CMD[2:0]), .b(3'b010), .eq(comparator_4_eq));  // open: gt, lt
  assign bit_extender_4_out = {{7{1'b1}}, comparator_4_eq};  // Bit_Extender bit_extender_4
  Register register_5 (.D(and_8_out), .en(and_9_out), .clk(clock_3_out), .Q(register_5_q), .clr(reset));
  Clock clock_3 (.out(clock_3_out));
  Register register_6 (.D(ool_out), .en(and_7_out), .clk(clock_4_out), .Q(register_6_q), .clr(reset));
  assign ool_out = {8{io}} & bit_extender_3_out & rd_result;  // AND_Gate ool, 8 bits wide
  Clock clock_4 (.out(clock_4_out));
  assign and_10_out = {8{io}} & bit_extender_4_out & undriven;  // AND_Gate and_10, 8 bits wide
  Comparator #(.width(3)) comparator_5 (.a(CMD[2:0]), .b(3'b011), .eq(comparator_5_eq));  // open: gt, lt
  assign bit_extender_5_out = {{7{1'b1}}, comparator_5_eq};  // Bit_Extender bit_extender_5
  // LedBar #(.inputtype("row")) ooo: pin names not known; wires that end beside it: register_5_q
  assign and_11_out = {8{io}} & bit_extender_5_out & button_2_out;  // AND_Gate and_11, 8 bits wide
  Hex_Digit_Display hex_digit_display_1 (.value(register_6_q[7:4]));  // open: dp
  Hex_Digit_Display hex_digit_display_2 (.value(register_6_q[3:0]));  // open: dp
  Multiplexer #(.width(8)) multiplexer_6 (.in0(and_11_out), .in1(and_10_out), .out(ioinput), .sel(comparator_4_eq));

  // Other names for the same wires on the sheet: idx[2:0] = CMD[2:0]; imm[1:0] = CMD[1:0]; rs2[1:0] = CMD[1:0];
  //   op_code[1:0] = CMD[7:6]; offset[3:0] = CMD[5:2]; rd[1:0] = CMD[5:4]; rs0_data[7:0] = r0_result;
  //   rs1[1:0] = CMD[3:2]; s[1:0] = CMD[3:2]; i_or_o = CMD[3]; sum[7:0] = r2_result

  // Notes on the sheet:
  //   CMD
  //   COUNTER
  //   contents of rom_1 (hex, n*v repeats v):
  //   42 b1 17 29 58 f5 81 73 ff 69 c1
  //   ROM
  //   op_code
endmodule
